// Logisim project counter.circ as structural Verilog: 3 circuits, main circuit main
module main (
);

  wire and_1_out, and_2_out, clock_1_out, j_k_ff_1_q, j_k_ff_2_q, j_k_ff_3_q, j_k_ff_4_q, j_k_ff_5_q,
       j_k_ff_6_q, j_k_ff_7_q, n7_segment_display_driver_1_a, n7_segment_display_driver_1_b,
       n7_segment_display_driver_1_c, n7_segment_display_driver_1_d, n7_segment_display_driver_1_e,
       n7_segment_display_driver_1_f, n7_segment_display_driver_1_g, n7_segment_display_driver_2_a,
       n7_segment_display_driver_2_b, n7_segment_display_driver_2_c, n7_segment_display_driver_2_d,
       n7_segment_display_driver_2_e, n7_segment_display_driver_2_f, n7_segment_display_driver_2_g,
       not_1_out, not_2_out, not_3_out, not_4_out, not_5_out, not_6_out, not_7_out, not_8_out, not_9_out,
       not_10_out, not_11_out, not_12_out;

  Clock clock_1 (.out(clock_1_out));
  LED led_1 (.in(j_k_ff_1_q));
  J_K_Flip_Flop j_k_ff_1 (.J(1'b1), .clk(clock_1_out), .K(1'b1), .Q(j_k_ff_1_q));  // open: Qn, preset, en, reset
  LED led_2 (.in(j_k_ff_2_q));
  J_K_Flip_Flop j_k_ff_2 (
    .J(1'b1), .clk(j_k_ff_1_q), .K(1'b1), .Q(j_k_ff_2_q), .reset(and_1_out));  // open: Qn, preset, en
  _7_segment_display_driver u_7_segment_display_driver_1 (
    .D0(j_k_ff_4_q), .D1(j_k_ff_3_q), .D2(j_k_ff_2_q), .D3(j_k_ff_1_q), .a(n7_segment_display_driver_1_a),
    .b(n7_segment_display_driver_1_b), .c(n7_segment_display_driver_1_c), .d(n7_segment_display_driver_1_d),
    .e(n7_segment_display_driver_1_e), .f(n7_segment_display_driver_1_f), .g(n7_segment_display_driver_1_g));
  _7_Segment_Display #(.active("false")) u_7_segment_display_1 (
    .g(n7_segment_display_driver_1_g), .f(n7_segment_display_driver_1_f), .a(n7_segment_display_driver_1_a),
    .b(n7_segment_display_driver_1_b), .e(n7_segment_display_driver_1_e), .d(n7_segment_display_driver_1_d),
    .c(n7_segment_display_driver_1_c));  // open: dp
  J_K_Flip_Flop j_k_ff_3 (
    .J(1'b1), .clk(j_k_ff_2_q), .K(1'b1), .Q(j_k_ff_3_q), .reset(and_1_out));  // open: Qn, preset, en
  LED led_3 (.in(j_k_ff_3_q));
  not not_1 (not_1_out, j_k_ff_3_q);
  not not_2 (not_2_out, not_1_out);
  not not_3 (not_3_out, not_2_out);
  not not_4 (not_4_out, not_3_out);
  J_K_Flip_Flop j_k_ff_4 (.J(1'b1), .clk(j_k_ff_3_q), .K(1'b1), .Q(j_k_ff_4_q));  // open: Qn, preset, en, reset
  LED led_4 (.in(j_k_ff_4_q));
  not not_5 (not_5_out, not_4_out);
  not not_6 (not_6_out, not_5_out);
  not not_7 (not_7_out, j_k_ff_6_q);
  J_K_Flip_Flop j_k_ff_5 (
    .J(1'b1), .clk(and_1_out), .K(1'b1), .Q(j_k_ff_5_q), .preset(and_2_out));  // open: Qn, en, reset
  and and_1 (and_1_out, not_6_out, j_k_ff_4_q);
  not not_8 (not_8_out, not_7_out);
  not not_9 (not_9_out, not_8_out);
  LED led_5 (.in(j_k_ff_5_q));
  _7_segment_display_driver u_7_segment_display_driver_2 (
    .D0(1'b0), .D1(j_k_ff_7_q), .D2(j_k_ff_6_q), .D3(j_k_ff_5_q), .a(n7_segment_display_driver_2_a),
    .b(n7_segment_display_driver_2_b), .c(n7_segment_display_driver_2_c), .d(n7_segment_display_driver_2_d),
    .e(n7_segment_display_driver_2_e), .f(n7_segment_display_driver_2_f), .g(n7_segment_display_driver_2_g));
  not not_10 (not_10_out, not_9_out);
  not not_11 (not_11_out, not_10_out);
  J_K_Flip_Flop j_k_ff_6 (
    .J(1'b1), .clk(j_k_ff_5_q), .K(1'b1), .Q(j_k_ff_6_q), .reset(and_2_out));  // open: Qn, preset, en
  LED led_6 (.in(j_k_ff_6_q));
  not not_12 (not_12_out, not_11_out);
  J_K_Flip_Flop j_k_ff_7 (
    .J(1'b1), .clk(j_k_ff_6_q), .K(1'b1), .Q(j_k_ff_7_q), .preset(and_2_out));  // open: Qn, en, reset
  LED led_7 (.in(j_k_ff_7_q));
  _7_Segment_Display #(.active("false")) u_7_segment_display_2 (
    .g(n7_segment_display_driver_2_g), .f(n7_segment_display_driver_2_f), .a(n7_segment_display_driver_2_a),
    .b(n7_segment_display_driver_2_b), .e(n7_segment_display_driver_2_e), .d(n7_segment_display_driver_2_d),
    .c(n7_segment_display_driver_2_c));  // open: dp
  and and_2 (and_2_out, not_12_out, j_k_ff_7_q);
endmodule

module _7_segment_display_driver (
  input  D0,
  input  D1,
  input  D2,
  input  D3,
  output a,
  output b,
  output c,
  output d,
  output e,
  output f,
  output g
);

  wire and_1_out, and_2_out, and_4_out, and_5_out, and_6_out, and_7_out, and_8_out, and_9_out, and_10_out,
       and_11_out, and_12_out, and_13_out, and_14_out, not_1_out, not_2_out, not_3_out, not_4_out, not_5_out,
       not_6_out, not_7_out, not_8_out, not_9_out, not_10_out, not_11_out, not_12_out, not_13_out,
       not_14_out, not_15_out, not_16_out, not_17_out, not_18_out, not_19_out, not_20_out, not_21_out;

  not not_1 (not_1_out, D0);
  not not_2 (not_2_out, D1);
  not not_3 (not_3_out, D2);
  not not_4 (not_4_out, D2);
  not not_5 (not_5_out, D3);
  and and_1 (and_1_out, D1, not_6_out, D3);
  not not_6 (not_6_out, D2);
  and and_2 (and_2_out, D1, D2, not_7_out);
  not not_7 (not_7_out, D3);
  not not_8 (not_8_out, D1);
  and and_3 (c, not_8_out, D2, not_9_out);
  not not_9 (not_9_out, D3);
  not not_10 (not_10_out, D0);
  not not_11 (not_11_out, D1);
  not not_12 (not_12_out, D2);
  not not_13 (not_13_out, D2);
  not not_14 (not_14_out, D3);
  and and_4 (and_4_out, D1, not_15_out);
  not not_15 (not_15_out, D2);
  not not_16 (not_16_out, D0);
  and and_5 (and_5_out, not_16_out, not_17_out, D3);
  not not_17 (not_17_out, D1);
  not not_18 (not_18_out, D1);
  and and_6 (and_6_out, not_18_out, D2);
  and and_7 (and_7_out, D2, D3);
  not not_19 (not_19_out, D0);
  not not_20 (not_20_out, D1);
  and and_8 (and_8_out, not_19_out, not_20_out, not_21_out);
  not not_21 (not_21_out, D2);
  and and_9 (and_9_out, D1, D2, D3);
  and and_10 (and_10_out, not_1_out, not_2_out, not_3_out, D3);
  or or_1 (a, and_10_out, and_11_out);
  and and_11 (and_11_out, D1, not_4_out, not_5_out);
  or or_2 (b, and_1_out, and_2_out);
  and and_12 (and_12_out, not_10_out, not_11_out, not_12_out, D3);
  or or_3 (d, and_12_out, and_13_out, and_14_out);
  and and_13 (and_13_out, D1, not_13_out, not_14_out);
  and and_14 (and_14_out, D1, D2, D3);
  or or_4 (e, D3, and_4_out);
  or or_5 (f, and_5_out, and_6_out, and_7_out);
  or or_6 (g, and_8_out, and_9_out);
endmodule

module sec_counter (
  output D0,
  output D1,
  output D2,
  output D3,
  output D4,
  output D5,
  output D6
);

  wire and_1_out, and_2_out, clock_1_out, not_1_out, not_2_out, not_3_out, not_4_out, not_5_out, not_6_out,
       not_7_out, not_8_out, not_9_out, not_10_out, not_11_out, not_12_out;

  Clock clock_1 (.out(clock_1_out));
  J_K_Flip_Flop j_k_ff_1 (.J(1'b1), .clk(clock_1_out), .K(1'b1), .Q(D0));  // open: Qn, preset, en, reset
  not not_1 (not_1_out, not_2_out);
  not not_2 (not_2_out, D5);
  J_K_Flip_Flop j_k_ff_2 (.J(1'b1), .clk(and_2_out), .K(1'b1), .Q(D4), .preset(and_1_out));  // open: Qn, en, reset
  not not_3 (not_3_out, not_4_out);
  not not_4 (not_4_out, not_1_out);
  J_K_Flip_Flop j_k_ff_3 (.J(1'b1), .clk(D4), .K(1'b1), .Q(D5), .reset(and_1_out));  // open: Qn, preset, en
  J_K_Flip_Flop j_k_ff_4 (.J(1'b1), .clk(D0), .K(1'b1), .Q(D1), .reset(and_2_out));  // open: Qn, preset, en
  not not_5 (not_5_out, not_3_out);
  not not_6 (not_6_out, not_5_out);
  J_K_Flip_Flop j_k_ff_5 (.J(1'b1), .clk(D5), .K(1'b1), .Q(D6), .preset(and_1_out));  // open: Qn, en, reset
  and and_1 (and_1_out, not_6_out, D6);
  J_K_Flip_Flop j_k_ff_6 (.J(1'b1), .clk(D1), .K(1'b1), .Q(D2), .reset(and_2_out));  // open: Qn, preset, en
  not not_7 (not_7_out, not_8_out);
  not not_8 (not_8_out, D2);
  not not_9 (not_9_out, not_7_out);
  not not_10 (not_10_out, not_9_out);
  J_K_Flip_Flop j_k_ff_7 (.J(1'b1), .clk(D2), .K(1'b1), .Q(D3));  // open: Qn, preset, en, reset
  not not_11 (not_11_out, not_10_out);
  not not_12 (not_12_out, not_11_out);
  and and_2 (and_2_out, not_12_out, D3);
endmodule
