// Logisim project counter1.circ as structural Verilog: 3 circuits, main circuit main
module main (
);

  wire sec_counter_1_a1_min, sec_counter_1_a1_sec, sec_counter_1_a_hr, sec_counter_1_a_min,
       sec_counter_1_a_sec, sec_counter_1_b1_min, sec_counter_1_b1_sec, sec_counter_1_b_hr,
       sec_counter_1_b_min, sec_counter_1_b_sec, sec_counter_1_c1_min, sec_counter_1_c1_sec,
       sec_counter_1_c_hr, sec_counter_1_c_min, sec_counter_1_c_sec, sec_counter_1_d1_min,
       sec_counter_1_d1_sec, sec_counter_1_d_hr, sec_counter_1_d_min, sec_counter_1_d_sec,
       sec_counter_1_e1_min, sec_counter_1_e1_sec, sec_counter_1_e_hr, sec_counter_1_e_min,
       sec_counter_1_e_sec, sec_counter_1_f1_min, sec_counter_1_f1_sec, sec_counter_1_f_hr,
       sec_counter_1_f_min, sec_counter_1_f_sec, sec_counter_1_g1_min, sec_counter_1_g1_sec,
       sec_counter_1_g_hr, sec_counter_1_g_min, sec_counter_1_g_sec;

  _7_Segment_Display #(.active("false")) u_7_segment_display_1 (
    .g(1'b1), .f(1'b0), .a(1'b0), .b(1'b0), .e(1'b0), .d(1'b0), .c(1'b0));  // open: dp
  _7_Segment_Display #(.active("false")) u_7_segment_display_2 (
    .g(sec_counter_1_g_hr), .f(sec_counter_1_f_hr), .a(sec_counter_1_a_hr), .b(sec_counter_1_b_hr),
    .e(sec_counter_1_e_hr), .d(sec_counter_1_d_hr), .c(sec_counter_1_c_hr));  // open: dp
  _7_Segment_Display #(.active("false")) u_7_segment_display_3 (
    .g(sec_counter_1_g1_min), .f(sec_counter_1_f1_min), .a(sec_counter_1_a1_min), .b(sec_counter_1_b1_min),
    .e(sec_counter_1_e1_min), .d(sec_counter_1_d1_min), .c(sec_counter_1_c1_min));  // open: dp
  _7_Segment_Display #(.active("false")) u_7_segment_display_4 (
    .g(sec_counter_1_g_min), .f(sec_counter_1_f_min), .a(sec_counter_1_a_min), .b(sec_counter_1_b_min),
    .e(sec_counter_1_e_min), .d(sec_counter_1_d_min), .c(sec_counter_1_c_min));  // open: dp
  _7_Segment_Display #(.active("false")) u_7_segment_display_5 (
    .g(sec_counter_1_g1_sec), .f(sec_counter_1_f1_sec), .a(sec_counter_1_a1_sec), .b(sec_counter_1_b1_sec),
    .e(sec_counter_1_e1_sec), .d(sec_counter_1_d1_sec), .c(sec_counter_1_c1_sec));  // open: dp
  sec_counter sec_counter_1 (
    .a_sec(sec_counter_1_a_sec), .b_sec(sec_counter_1_b_sec), .c_sec(sec_counter_1_c_sec),
    .d_sec(sec_counter_1_d_sec), .e_sec(sec_counter_1_e_sec), .f_sec(sec_counter_1_f_sec),
    .g_sec(sec_counter_1_g_sec), .a1_sec(sec_counter_1_a1_sec), .b1_sec(sec_counter_1_b1_sec),
    .c1_sec(sec_counter_1_c1_sec), .d1_sec(sec_counter_1_d1_sec), .e1_sec(sec_counter_1_e1_sec),
    .f1_sec(sec_counter_1_f1_sec), .g1_sec(sec_counter_1_g1_sec), .a_min(sec_counter_1_a_min),
    .b_min(sec_counter_1_b_min), .c_min(sec_counter_1_c_min), .d_min(sec_counter_1_d_min),
    .e_min(sec_counter_1_e_min), .f_min(sec_counter_1_f_min), .g_min(sec_counter_1_g_min),
    .a1_min(sec_counter_1_a1_min), .b1_min(sec_counter_1_b1_min), .c1_min(sec_counter_1_c1_min),
    .d1_min(sec_counter_1_d1_min), .e1_min(sec_counter_1_e1_min), .f1_min(sec_counter_1_f1_min),
    .g1_min(sec_counter_1_g1_min), .a_hr(sec_counter_1_a_hr), .b_hr(sec_counter_1_b_hr),
    .c_hr(sec_counter_1_c_hr), .d_hr(sec_counter_1_d_hr), .e_hr(sec_counter_1_e_hr),
    .f_hr(sec_counter_1_f_hr), .g_hr(sec_counter_1_g_hr));  // open: in_1
  _7_Segment_Display #(.active("false")) u_7_segment_display_6 (
    .g(sec_counter_1_g_sec), .f(sec_counter_1_f_sec), .a(sec_counter_1_a_sec), .b(sec_counter_1_b_sec),
    .e(sec_counter_1_e_sec), .d(sec_counter_1_d_sec), .c(sec_counter_1_c_sec));  // open: dp
endmodule

module BCD_to_7seg (
  input  D3,
  input  D2,
  input  D1,
  input  D0,
  output a,
  output b,
  output c,
  output d,
  output e,
  output f,
  output g
);

  wire and_1_out, and_2_out, and_3_out, and_4_out, and_5_out, and_6_out, and_7_out, and_8_out, and_9_out,
       and_10_out, and_11_out, and_12_out, and_13_out, and_14_out, and_15_out, and_16_out, and_17_out,
       and_18_out, and_19_out, and_20_out, and_21_out, and_22_out, not_1_out, not_2_out, not_3_out,
       not_4_out, not_5_out, not_6_out, not_7_out, not_8_out, not_9_out, not_10_out, not_11_out, not_12_out,
       not_13_out, not_14_out, not_15_out, not_16_out, not_17_out, not_18_out, not_19_out, not_20_out,
       not_21_out;

  not not_1 (not_1_out, D3);
  not not_2 (not_2_out, D2);
  not not_3 (not_3_out, D1);
  not not_4 (not_4_out, D1);
  not not_5 (not_5_out, D0);
  and and_1 (and_1_out, D2, not_6_out, D0);
  not not_6 (not_6_out, D1);
  and and_2 (and_2_out, D2, D1, not_7_out);
  not not_7 (not_7_out, D0);
  and and_3 (and_3_out, D3, D1);
  not not_8 (not_8_out, D2);
  and and_4 (and_4_out, not_8_out, D1, not_9_out);
  not not_9 (not_9_out, D0);
  and and_5 (and_5_out, D3, D2);
  not not_10 (not_10_out, D3);
  not not_11 (not_11_out, D2);
  not not_12 (not_12_out, D1);
  not not_13 (not_13_out, D1);
  not not_14 (not_14_out, D0);
  and and_6 (and_6_out, D2, not_15_out);
  not not_15 (not_15_out, D1);
  and and_7 (and_7_out, D3, D1);
  not not_16 (not_16_out, D3);
  not not_17 (not_17_out, D2);
  and and_8 (and_8_out, not_16_out, not_17_out, D0);
  not not_18 (not_18_out, D2);
  and and_9 (and_9_out, not_18_out, D1);
  and and_10 (and_10_out, D1, D0);
  and and_11 (and_11_out, D3, D2);
  not not_19 (not_19_out, D3);
  not not_20 (not_20_out, D2);
  and and_12 (and_12_out, not_19_out, not_20_out, not_21_out);
  not not_21 (not_21_out, D1);
  and and_13 (and_13_out, D2, D1, D0);
  and and_14 (and_14_out, D3, D1);
  and and_15 (and_15_out, D3, D2);
  and and_16 (and_16_out, not_1_out, not_2_out, not_3_out, D0);
  or or_1 (a, and_16_out, and_17_out, and_18_out);
  and and_17 (and_17_out, D2, not_4_out, not_5_out);
  and and_18 (and_18_out, D3, D2);
  or or_2 (b, and_1_out, and_2_out, and_3_out);
  or or_3 (c, and_4_out, and_5_out);
  and and_19 (and_19_out, not_10_out, not_11_out, not_12_out, D0);
  and and_20 (and_20_out, D2, not_13_out, not_14_out);
  and and_21 (and_21_out, D2, D1, D0);
  and and_22 (and_22_out, D3, D2);
  or or_4 (e, D0, and_6_out, and_7_out);
  or or_5 (f, and_8_out, and_9_out, and_10_out, and_11_out);
  or or_6 (g, and_12_out, and_13_out, and_14_out, and_15_out);
  or or_7 (d, and_19_out, and_20_out, and_21_out, and_22_out);
endmodule

module sec_counter (
  input  in_1,
  output a_sec,
  output b_sec,
  output c_sec,
  output d_sec,
  output e_sec,
  output f_sec,
  output g_sec,
  output a1_sec,
  output b1_sec,
  output c1_sec,
  output d1_sec,
  output e1_sec,
  output f1_sec,
  output g1_sec,
  output a_min,
  output b_min,
  output c_min,
  output d_min,
  output e_min,
  output f_min,
  output g_min,
  output a1_min,
  output b1_min,
  output c1_min,
  output d1_min,
  output e1_min,
  output f1_min,
  output g1_min,
  output a_hr,
  output b_hr,
  output c_hr,
  output d_hr,
  output e_hr,
  output f_hr,
  output g_hr
);

  wire and_1_out, and_2_out, and_3_out, and_4_out, clock_1_out, j_k_ff_1_q, j_k_ff_2_q, j_k_ff_3_q,
       j_k_ff_4_q, j_k_ff_5_q, j_k_ff_6_q, j_k_ff_7_q, j_k_ff_8_q, j_k_ff_9_q, j_k_ff_10_q, j_k_ff_11_q,
       j_k_ff_12_q, j_k_ff_13_q, j_k_ff_14_q, j_k_ff_15_q, j_k_ff_16_q, not_1_out, not_2_out, not_3_out,
       not_4_out, not_5_out, not_6_out, not_7_out, not_8_out, not_9_out, not_10_out, not_11_out, not_12_out,
       not_13_out, not_14_out, not_15_out, not_16_out, not_17_out, not_18_out, not_19_out, not_20_out,
       not_21_out, not_22_out, not_23_out, not_24_out, t_ff_1_q, transistor_1_out;

  Clock clock_1 (.out(clock_1_out));
  T_Flip_Flop t_ff_1 (.clk(in_1), .T(in_1), .Q(t_ff_1_q));  // open: Qn, preset, reset, en
  Transistor #(.\type ("n")) transistor_1 (.in(clock_1_out), .out(transistor_1_out), .gate(t_ff_1_q));
  J_K_Flip_Flop j_k_ff_1 (.J(1'b1), .clk(transistor_1_out), .K(1'b1), .Q(j_k_ff_1_q));  // open: Qn, preset, en, reset
  not not_1 (not_1_out, j_k_ff_6_q);
  J_K_Flip_Flop j_k_ff_2 (
    .J(1'b1), .clk(and_3_out), .K(1'b1), .Q(j_k_ff_2_q), .preset(and_1_out));  // open: Qn, en, reset
  J_K_Flip_Flop j_k_ff_3 (.J(1'b1), .clk(and_1_out), .K(1'b1), .Q(j_k_ff_3_q));  // open: Qn, preset, en, reset
  not not_2 (not_2_out, j_k_ff_9_q);
  J_K_Flip_Flop j_k_ff_4 (
    .J(1'b1), .clk(and_4_out), .K(1'b1), .Q(j_k_ff_4_q), .preset(and_2_out));  // open: Qn, en, reset
  J_K_Flip_Flop j_k_ff_5 (
    .J(1'b1), .clk(and_2_out), .K(1'b1), .Q(j_k_ff_5_q), .preset(j_k_ff_10_q));  // open: Qn, en, reset
  not not_3 (not_3_out, not_4_out);
  not not_4 (not_4_out, not_1_out);
  J_K_Flip_Flop j_k_ff_6 (
    .J(1'b1), .clk(j_k_ff_2_q), .K(1'b1), .Q(j_k_ff_6_q), .reset(and_1_out));  // open: Qn, preset, en
  not not_5 (not_5_out, not_6_out);
  not not_6 (not_6_out, not_2_out);
  J_K_Flip_Flop j_k_ff_7 (
    .J(1'b1), .clk(j_k_ff_1_q), .K(1'b1), .Q(j_k_ff_7_q), .reset(and_3_out));  // open: Qn, preset, en
  not not_7 (not_7_out, not_3_out);
  not not_8 (not_8_out, not_7_out);
  J_K_Flip_Flop j_k_ff_8 (
    .J(1'b1), .clk(j_k_ff_3_q), .K(1'b1), .Q(j_k_ff_8_q), .reset(and_4_out));  // open: Qn, preset, en
  not not_9 (not_9_out, not_10_out);
  not not_10 (not_10_out, not_5_out);
  J_K_Flip_Flop j_k_ff_9 (
    .J(1'b1), .clk(j_k_ff_4_q), .K(1'b1), .Q(j_k_ff_9_q), .reset(and_2_out));  // open: Qn, preset, en
  J_K_Flip_Flop j_k_ff_10 (
    .J(1'b1), .clk(j_k_ff_5_q), .K(1'b1), .Q(j_k_ff_10_q), .reset(j_k_ff_10_q));  // open: Qn, preset, en
  not not_11 (not_11_out, not_8_out);
  and and_1 (and_1_out, not_11_out, j_k_ff_11_q);
  J_K_Flip_Flop j_k_ff_11 (
    .J(1'b1), .clk(j_k_ff_6_q), .K(1'b1), .Q(j_k_ff_11_q), .preset(and_1_out));  // open: Qn, en, reset
  not not_12 (not_12_out, not_9_out);
  J_K_Flip_Flop j_k_ff_12 (
    .J(1'b1), .clk(j_k_ff_9_q), .K(1'b1), .Q(j_k_ff_12_q), .preset(and_2_out));  // open: Qn, en, reset
  J_K_Flip_Flop j_k_ff_13 (
    .J(1'b1), .clk(j_k_ff_7_q), .K(1'b1), .Q(j_k_ff_13_q), .reset(and_3_out));  // open: Qn, preset, en
  and and_2 (and_2_out, not_12_out, j_k_ff_12_q);
  BCD_to_7seg bcd_to_7seg_1 (
    .D3(1'b0), .D2(1'b0), .D1(j_k_ff_10_q), .D0(j_k_ff_5_q), .a(a_hr), .b(b_hr), .c(c_hr), .d(d_hr),
    .e(e_hr), .f(f_hr), .g(g_hr));
  not not_13 (not_13_out, j_k_ff_13_q);
  BCD_to_7seg bcd_to_7seg_2 (
    .D3(1'b0), .D2(j_k_ff_11_q), .D1(j_k_ff_6_q), .D0(j_k_ff_2_q), .a(a1_sec), .b(b1_sec), .c(c1_sec),
    .d(d1_sec), .e(e1_sec), .f(f1_sec), .g(g1_sec));
  not not_14 (not_14_out, j_k_ff_14_q);
  J_K_Flip_Flop j_k_ff_14 (
    .J(1'b1), .clk(j_k_ff_8_q), .K(1'b1), .Q(j_k_ff_14_q), .reset(and_4_out));  // open: Qn, preset, en
  BCD_to_7seg bcd_to_7seg_3 (
    .D3(1'b0), .D2(j_k_ff_12_q), .D1(j_k_ff_9_q), .D0(j_k_ff_4_q), .a(a1_min), .b(b1_min), .c(c1_min),
    .d(d1_min), .e(e1_min), .f(f1_min), .g(g1_min));
  not not_15 (not_15_out, not_16_out);
  not not_16 (not_16_out, not_13_out);
  BCD_to_7seg bcd_to_7seg_4 (
    .D3(j_k_ff_15_q), .D2(j_k_ff_13_q), .D1(j_k_ff_7_q), .D0(j_k_ff_1_q), .a(a_sec), .b(b_sec), .c(c_sec),
    .d(d_sec), .e(e_sec), .f(f_sec), .g(g_sec));
  not not_17 (not_17_out, not_14_out);
  not not_18 (not_18_out, not_17_out);
  BCD_to_7seg bcd_to_7seg_5 (
    .D3(j_k_ff_16_q), .D2(j_k_ff_14_q), .D1(j_k_ff_8_q), .D0(j_k_ff_3_q), .a(a_min), .b(b_min), .c(c_min),
    .d(d_min), .e(e_min), .f(f_min), .g(g_min));
  not not_19 (not_19_out, not_15_out);
  not not_20 (not_20_out, not_19_out);
  J_K_Flip_Flop j_k_ff_15 (.J(1'b1), .clk(j_k_ff_13_q), .K(1'b1), .Q(j_k_ff_15_q));  // open: Qn, preset, en, reset
  not not_21 (not_21_out, not_18_out);
  not not_22 (not_22_out, not_21_out);
  J_K_Flip_Flop j_k_ff_16 (.J(1'b1), .clk(j_k_ff_14_q), .K(1'b1), .Q(j_k_ff_16_q));  // open: Qn, preset, en, reset
  not not_23 (not_23_out, not_20_out);
  not not_24 (not_24_out, not_22_out);
  and and_3 (and_3_out, not_23_out, j_k_ff_15_q);
  and and_4 (and_4_out, not_24_out, j_k_ff_16_q);
endmodule
