// Logisim project test1.circ as structural Verilog: 2 circuits, main circuit main
module main (
);

  wire button_1_out, clock_1_out, convert_bcd_1_a, convert_bcd_1_b, convert_bcd_1_c, convert_bcd_1_d,
       convert_bcd_1_e, convert_bcd_1_f, convert_bcd_1_g, j_k_ff_1_q, j_k_ff_1_qn, j_k_ff_2_q, j_k_ff_2_qn,
       j_k_ff_3_q, j_k_ff_3_qn, j_k_ff_4_q, multiplexer_1_out, multiplexer_2_out, multiplexer_3_out,
       not_1_out, t_ff_1_q;

  Button button_1 (.out(button_1_out));
  Clock clock_1 (.out(clock_1_out));
  T_Flip_Flop t_ff_1 (.clk(button_1_out), .T(button_1_out), .Q(t_ff_1_q));  // open: Qn, preset, reset, en
  not not_1 (not_1_out, t_ff_1_q);
  J_K_Flip_Flop #(.trigger("falling")) j_k_ff_1 (
    .J(1'b1), .clk(clock_1_out), .K(1'b1), .Q(j_k_ff_1_q), .Qn(j_k_ff_1_qn));  // open: preset, en, reset
  Multiplexer multiplexer_1 (
    .in0(j_k_ff_1_q), .in1(j_k_ff_1_qn), .out(multiplexer_1_out), .sel(not_1_out));  // open: en
  J_K_Flip_Flop #(.trigger("falling")) j_k_ff_2 (
    .J(1'b1), .clk(multiplexer_1_out), .K(1'b1), .Q(j_k_ff_2_q), .Qn(j_k_ff_2_qn));  // open: preset, en, reset
  Multiplexer multiplexer_2 (
    .in0(j_k_ff_2_q), .in1(j_k_ff_2_qn), .out(multiplexer_2_out), .sel(not_1_out));  // open: en
  J_K_Flip_Flop #(.trigger("falling")) j_k_ff_3 (
    .J(1'b1), .clk(multiplexer_2_out), .K(1'b1), .Q(j_k_ff_3_q), .Qn(j_k_ff_3_qn));  // open: preset, en, reset
  convert_bcd convert_bcd_1 (
    .D3(j_k_ff_4_q), .D2(j_k_ff_3_q), .D1(j_k_ff_2_q), .D0(j_k_ff_1_q), .a(convert_bcd_1_a),
    .b(convert_bcd_1_b), .c(convert_bcd_1_c), .d(convert_bcd_1_d), .e(convert_bcd_1_e), .f(convert_bcd_1_f),
    .g(convert_bcd_1_g));
  _7_Segment_Display #(.active("false")) u_7_segment_display_1 (
    .g(convert_bcd_1_g), .f(convert_bcd_1_f), .a(convert_bcd_1_a), .b(convert_bcd_1_b), .e(convert_bcd_1_e),
    .d(convert_bcd_1_d), .c(convert_bcd_1_c));  // open: dp
  Multiplexer multiplexer_3 (
    .in0(j_k_ff_3_q), .in1(j_k_ff_3_qn), .out(multiplexer_3_out), .sel(not_1_out));  // open: en
  J_K_Flip_Flop #(.trigger("falling")) j_k_ff_4 (
    .J(1'b1), .clk(multiplexer_3_out), .K(1'b1), .Q(j_k_ff_4_q));  // open: Qn, preset, en, reset
endmodule

module convert_bcd (
  input  D3,
  input  D2,
  input  D1,
  input  D0,
  output a,
  output b,
  output c,
  output d,
  output e,
  output f,
  output g
);

  wire and_1_out, and_2_out, and_3_out, and_4_out, and_5_out, and_6_out, and_7_out, and_8_out, and_9_out,
       and_10_out, and_11_out, and_12_out, and_13_out, and_14_out, and_15_out, and_16_out, and_17_out,
       and_18_out, and_19_out, and_20_out, and_21_out, and_22_out, and_23_out, and_24_out, and_25_out,
       not_1_out, not_2_out, not_3_out, not_4_out, not_5_out, not_6_out, not_7_out, not_8_out, not_9_out,
       not_10_out, not_11_out, not_12_out, not_13_out, not_14_out, not_15_out, not_16_out, not_17_out,
       not_18_out, not_19_out, not_20_out, not_21_out, not_22_out, not_23_out, not_24_out, not_25_out,
       not_26_out, not_27_out, not_28_out, not_29_out, not_30_out, not_31_out, not_32_out, not_33_out,
       not_34_out, not_35_out, not_36_out, not_37_out, not_38_out, not_39_out, not_40_out, not_41_out;

  not not_1 (not_1_out, D3);
  not not_2 (not_2_out, D2);
  not not_3 (not_3_out, D1);
  not not_4 (not_4_out, D3);
  not not_5 (not_5_out, D1);
  not not_6 (not_6_out, D0);
  not not_7 (not_7_out, D2);
  not not_8 (not_8_out, D1);
  not not_9 (not_9_out, D3);
  not not_10 (not_10_out, D1);
  not not_11 (not_11_out, D0);
  not not_12 (not_12_out, D0);
  not not_13 (not_13_out, D3);
  not not_14 (not_14_out, D2);
  not not_15 (not_15_out, D0);
  not not_16 (not_16_out, D0);
  not not_17 (not_17_out, D3);
  not not_18 (not_18_out, D2);
  not not_19 (not_19_out, D1);
  not not_20 (not_20_out, D3);
  not not_21 (not_21_out, D1);
  not not_22 (not_22_out, D0);
  not not_23 (not_23_out, D2);
  not not_24 (not_24_out, D0);
  not not_25 (not_25_out, D3);
  and and_1 (and_1_out, not_25_out, D0);
  not not_26 (not_26_out, D2);
  and and_2 (and_2_out, not_26_out, not_27_out, D0);
  not not_27 (not_27_out, D1);
  not not_28 (not_28_out, D3);
  and and_3 (and_3_out, not_28_out, D2, not_29_out);
  not not_29 (not_29_out, D1);
  not not_30 (not_30_out, D3);
  not not_31 (not_31_out, D2);
  not not_32 (not_32_out, D3);
  not not_33 (not_33_out, D2);
  not not_34 (not_34_out, D3);
  not not_35 (not_35_out, D1);
  not not_36 (not_36_out, D3);
  not not_37 (not_37_out, D2);
  not not_38 (not_38_out, D1);
  not not_39 (not_39_out, D3);
  not not_40 (not_40_out, D1);
  not not_41 (not_41_out, D0);
  and and_4 (and_4_out, not_1_out, not_2_out, not_3_out, D0);
  and and_5 (and_5_out, not_4_out, D2, not_5_out, not_6_out);
  and and_6 (and_6_out, D3, not_7_out, D1, D0);
  and and_7 (and_7_out, D3, D2, not_8_out, D0);
  and and_8 (and_8_out, not_9_out, D2, not_10_out, D0);
  and and_9 (and_9_out, D2, D1, not_11_out);
  and and_10 (and_10_out, D3, D1, D0);
  and and_11 (and_11_out, D3, D2, not_12_out);
  and and_12 (and_12_out, not_13_out, not_14_out, D1, not_15_out);
  and and_13 (and_13_out, D3, D2, not_16_out);
  or or_1 (c, and_12_out, and_13_out, and_14_out);
  and and_14 (and_14_out, D3, D2, D1);
  and and_15 (and_15_out, not_17_out, not_18_out, not_19_out, D0);
  and and_16 (and_16_out, not_20_out, D2, not_21_out, not_22_out);
  and and_17 (and_17_out, D2, D1, D0);
  and and_18 (and_18_out, D3, not_23_out, D1, not_24_out);
  or or_2 (e, and_1_out, and_2_out, and_3_out);
  and and_19 (and_19_out, not_30_out, not_31_out, D0);
  and and_20 (and_20_out, not_32_out, not_33_out, D1);
  and and_21 (and_21_out, not_34_out, D1, D0);
  and and_22 (and_22_out, D3, D2, not_35_out, D0);
  and and_23 (and_23_out, not_36_out, not_37_out, not_38_out);
  and and_24 (and_24_out, not_39_out, D2, D1, D0);
  or or_3 (g, and_23_out, and_24_out, and_25_out);
  and and_25 (and_25_out, D3, D2, not_40_out, not_41_out);
  or or_4 (a, and_4_out, and_5_out, and_6_out, and_7_out);
  or or_5 (b, and_8_out, and_9_out, and_10_out, and_11_out);
  or or_6 (d, and_15_out, and_16_out, and_17_out, and_18_out);
  or or_7 (f, and_19_out, and_20_out, and_21_out, and_22_out);
endmodule
