// Logisim project up_down_counter.circ as structural Verilog: 13 circuits, main circuit main
module main (
);

  wire and_1_out, and_2_out, and_3_out, and_4_out, and_5_out, and_6_out, and_7_out, and_8_out, and_9_out,
       and_10_out, and_11_out, and_12_out, and_13_out, and_14_out, and_15_out, and_16_out, and_17_out,
       and_18_out, and_19_out, and_20_out, and_21_out, and_22_out, and_23_out, and_24_out, clock_1_out,
       clock_2_out, convert_bcd_1_a, convert_bcd_1_b, convert_bcd_1_c, convert_bcd_1_d, convert_bcd_1_e,
       convert_bcd_1_f, convert_bcd_1_g, convert_bcd_2_a, convert_bcd_2_b, convert_bcd_2_c, convert_bcd_2_d,
       convert_bcd_2_e, convert_bcd_2_f, convert_bcd_2_g, convert_bcd_3_a, convert_bcd_3_b, convert_bcd_3_c,
       convert_bcd_3_d, convert_bcd_3_e, convert_bcd_3_f, convert_bcd_3_g, convert_bcd_4_a, convert_bcd_4_b,
       convert_bcd_4_c, convert_bcd_4_d, convert_bcd_4_e, convert_bcd_4_f, convert_bcd_4_g, inc_2_out,
       inc_out, not_1_out, not_2_out, or_1_out, or_2_out, or_3_out, or_4_out, or_5_out, or_6_out, or_7_out,
       or_8_out, or_9_out, or_10_out, or_11_out, or_12_out, pull_resistor_2_node, RESET, reset_2_out,
       set_min_out, set_sec_out, start_2_out, start_out, switch_1_out_4, switch_2_out_4, switch_3_out_4,
       switch_4_out_4, switch_5_out_4, switch_6_out_4, switch_7_out_4, switch_8_out_4, t_ff_1_q, t_ff_2_q,
       t_ff_3_q, t_ff_4_q, t_ff_5_q, t_ff_6_q, t_ff_7_q, t_ff_8_q, t_ff_9_q, t_ff_10_q, t_ff_11_q, t_ff_12_q,
       t_ff_13_q, t_ff_14_q, t_ff_15_q, t_ff_16_q, t_ff_17_q, t_ff_18_q, t_ff_19_q, t_ff_20_q, t_ff_21_q,
       t_ff_22_q, t_ff_23_q, t_ff_24_q, transistor_1_out;

  Button set_sec (.out(set_sec_out));
  Button u_RESET (.out(RESET));
  Button reset_2 (.out(reset_2_out));
  Button inc (.out(inc_out));
  T_Flip_Flop t_ff_1 (.clk(set_sec_out), .T(set_sec_out), .Q(t_ff_1_q));  // open: Qn, preset, reset, en
  T_Flip_Flop t_ff_2 (.clk(inc_out), .T(inc_out), .Q(t_ff_2_q));  // open: Qn, preset, reset, en
  Button set_min (.out(set_min_out));
  T_Flip_Flop t_ff_3 (.clk(set_min_out), .T(set_min_out), .Q(t_ff_3_q));  // open: Qn, preset, reset, en
  T_Flip_Flop t_ff_4 (.clk(set_sec_out), .T(set_sec_out), .Q(t_ff_4_q));  // open: Qn, preset, reset, en
  T_Flip_Flop t_ff_5 (.clk(set_sec_out), .T(set_sec_out), .Q(t_ff_5_q));  // open: Qn, preset, reset, en
  switch switch_1 (.in_1(1'b0), .in_2(t_ff_1_q), .in_3(1'b1), .out_4(switch_1_out_4));
  not not_1 (not_1_out, t_ff_2_q);
  switch switch_2 (.in_1(and_16_out), .in_2(t_ff_5_q), .in_3(not_1_out), .out_4(switch_2_out_4));
  T_Flip_Flop t_ff_6 (.clk(set_min_out), .T(set_min_out), .Q(t_ff_6_q));  // open: Qn, preset, reset, en
  T_Flip_Flop t_ff_7 (.clk(set_min_out), .T(set_min_out), .Q(t_ff_7_q));  // open: Qn, preset, reset, en
  Button inc_2 (.out(inc_2_out));
  not not_2 (not_2_out, t_ff_8_q);
  T_Flip_Flop t_ff_8 (.clk(inc_2_out), .T(inc_2_out), .Q(t_ff_8_q));  // open: Qn, preset, reset, en
  switch switch_3 (.in_1(1'b0), .in_2(t_ff_4_q), .in_3(1'b1), .out_4(switch_3_out_4));
  T_Flip_Flop t_ff_9 (.clk(switch_7_out_4), .T(1'b1), .Q(t_ff_9_q), .reset(RESET));  // open: Qn, preset, en
  Button start (.out(start_out));
  T_Flip_Flop t_ff_10 (.clk(switch_2_out_4), .T(1'b1), .Q(t_ff_10_q), .reset(and_18_out));  // open: Qn, preset, en
  switch switch_4 (.in_1(1'b0), .in_2(t_ff_6_q), .in_3(1'b1), .out_4(switch_4_out_4));
  T_Flip_Flop t_ff_11 (.clk(switch_8_out_4), .T(1'b1), .Q(t_ff_11_q), .reset(reset_2_out));  // open: Qn, preset, en
  switch switch_5 (.in_1(1'b0), .in_2(t_ff_3_q), .in_3(1'b1), .out_4(switch_5_out_4));
  T_Flip_Flop t_ff_12 (.clk(switch_6_out_4), .T(1'b1), .Q(t_ff_12_q), .reset(and_23_out));  // open: Qn, preset, en
  switch switch_6 (.in_1(and_21_out), .in_2(t_ff_7_q), .in_3(not_2_out), .out_4(switch_6_out_4));
  and and_1 (and_1_out, ~switch_3_out_4, ~t_ff_9_q);  // AND_Gate
  Clock clock_1 (.out(clock_1_out));
  T_Flip_Flop t_ff_13 (.clk(start_out), .T(start_out), .Q(t_ff_13_q));  // open: Qn, preset, reset, en
  Transistor #(.\type ("n")) transistor_1 (.in(clock_1_out), .out(transistor_1_out), .gate(t_ff_13_q));
  and and_2 (and_2_out, ~switch_1_out_4, ~t_ff_10_q);  // AND_Gate
  and and_3 (and_3_out, switch_1_out_4, t_ff_10_q);
  T_Flip_Flop t_ff_14 (.clk(start_2_out), .T(start_2_out), .Q(t_ff_14_q));  // open: Qn, preset, reset, en
  Button start_2 (.out(start_2_out));
  T_Flip_Flop t_ff_15 (.clk(switch_7_out_4), .T(and_1_out), .Q(t_ff_15_q), .reset(or_1_out));  // open: Qn, preset, en
  or or_1 (or_1_out, RESET, and_16_out);
  Pull_Resistor pull_resistor_1 (.node(transistor_1_out));
  or or_2 (or_2_out, and_2_out, and_3_out);
  and and_4 (and_4_out, ~switch_4_out_4, ~t_ff_11_q);  // AND_Gate
  Clock clock_2 (.out(clock_2_out));
  Pull_Resistor pull_resistor_2 (.node(pull_resistor_2_node));
  Transistor #(.\type ("n")) transistor_2 (.in(clock_2_out), .out(pull_resistor_2_node), .gate(t_ff_14_q));
  and and_5 (and_5_out, ~switch_5_out_4, ~t_ff_12_q);  // AND_Gate
  or or_3 (or_3_out, and_5_out, and_6_out);
  and and_6 (and_6_out, switch_5_out_4, t_ff_12_q);
  and and_7 (and_7_out, ~t_ff_9_q, ~t_ff_15_q);  // AND_Gate
  switch switch_7 (.in_1(transistor_1_out), .in_2(t_ff_5_q), .in_3(inc_out), .out_4(switch_7_out_4));
  T_Flip_Flop t_ff_16 (.clk(switch_2_out_4), .T(or_2_out), .Q(t_ff_16_q), .reset(or_4_out));  // open: Qn, preset, en
  or or_4 (or_4_out, and_19_out, and_18_out);
  T_Flip_Flop t_ff_17 (.clk(switch_8_out_4), .T(and_4_out), .Q(t_ff_17_q), .reset(or_5_out));  // open: Qn, preset, en
  or or_5 (or_5_out, reset_2_out, and_21_out);
  or or_6 (or_6_out, and_24_out, and_23_out);
  or or_7 (or_7_out, and_7_out, switch_3_out_4);
  T_Flip_Flop t_ff_18 (.clk(switch_7_out_4), .T(or_7_out), .Q(t_ff_18_q), .reset(or_8_out));  // open: Qn, preset, en
  or or_8 (or_8_out, RESET, and_16_out);
  and and_8 (and_8_out, ~switch_1_out_4, ~t_ff_10_q, ~t_ff_16_q);  // AND_Gate
  and and_9 (and_9_out, switch_1_out_4, t_ff_10_q, t_ff_16_q);
  and and_10 (and_10_out, ~t_ff_11_q, ~t_ff_17_q);  // AND_Gate
  or or_9 (or_9_out, and_10_out, switch_4_out_4);
  or or_10 (or_10_out, reset_2_out, and_21_out);
  switch switch_8 (.in_1(pull_resistor_2_node), .in_2(t_ff_7_q), .in_3(inc_2_out), .out_4(switch_8_out_4));
  T_Flip_Flop t_ff_19 (.clk(switch_6_out_4), .T(or_3_out), .Q(t_ff_19_q), .reset(or_6_out));  // open: Qn, preset, en
  or or_11 (or_11_out, and_8_out, and_9_out);
  T_Flip_Flop t_ff_20 (.clk(switch_8_out_4), .T(or_9_out), .Q(t_ff_20_q), .reset(or_10_out));  // open: Qn, preset, en
  and and_11 (and_11_out, ~switch_5_out_4, ~t_ff_12_q, ~t_ff_19_q);  // AND_Gate
  or or_12 (or_12_out, and_11_out, and_12_out);
  and and_12 (and_12_out, switch_5_out_4, t_ff_12_q, t_ff_19_q);
  and and_13 (and_13_out, ~switch_3_out_4, ~t_ff_9_q, ~t_ff_15_q, ~t_ff_18_q);  // AND_Gate
  T_Flip_Flop t_ff_21 (.clk(switch_7_out_4), .T(and_13_out), .Q(t_ff_21_q), .reset(RESET));  // open: Qn, preset, en
  T_Flip_Flop t_ff_22 (.clk(switch_2_out_4), .T(or_11_out), .Q(t_ff_22_q), .reset(and_18_out));  // open: Qn, preset, en
  and and_14 (and_14_out, ~switch_4_out_4, ~t_ff_11_q, ~t_ff_17_q, ~t_ff_20_q);  // AND_Gate
  T_Flip_Flop t_ff_23 (
    .clk(switch_8_out_4), .T(and_14_out), .Q(t_ff_23_q), .reset(reset_2_out));  // open: Qn, preset, en
  and and_15 (and_15_out, t_ff_15_q, t_ff_21_q);
  and and_16 (and_16_out, ~switch_3_out_4, and_15_out);  // AND_Gate
  and and_17 (and_17_out, t_ff_16_q, t_ff_22_q);
  and and_18 (and_18_out, switch_1_out_4, and_17_out);
  and and_19 (and_19_out, ~switch_1_out_4, and_17_out);  // AND_Gate
  and and_20 (and_20_out, t_ff_17_q, t_ff_23_q);
  and and_21 (and_21_out, ~switch_4_out_4, and_20_out);  // AND_Gate
  T_Flip_Flop t_ff_24 (.clk(switch_6_out_4), .T(or_12_out), .Q(t_ff_24_q), .reset(and_23_out));  // open: Qn, preset, en
  and and_22 (and_22_out, t_ff_19_q, t_ff_24_q);
  and and_23 (and_23_out, switch_5_out_4, and_22_out);
  and and_24 (and_24_out, ~switch_5_out_4, and_22_out);  // AND_Gate
  convert_bcd convert_bcd_1 (
    .D3(t_ff_21_q), .D2(t_ff_18_q), .D1(t_ff_15_q), .D0(t_ff_9_q), .a(convert_bcd_1_a), .b(convert_bcd_1_b),
    .c(convert_bcd_1_c), .d(convert_bcd_1_d), .e(convert_bcd_1_e), .f(convert_bcd_1_f), .g(convert_bcd_1_g));
  convert_bcd convert_bcd_2 (
    .D3(1'b0), .D2(t_ff_22_q), .D1(t_ff_16_q), .D0(t_ff_10_q), .a(convert_bcd_2_a), .b(convert_bcd_2_b),
    .c(convert_bcd_2_c), .d(convert_bcd_2_d), .e(convert_bcd_2_e), .f(convert_bcd_2_f), .g(convert_bcd_2_g));
  _7_Segment_Display #(.active("false")) u_7_segment_display_1 (
    .g(convert_bcd_1_g), .f(convert_bcd_1_f), .a(convert_bcd_1_a), .b(convert_bcd_1_b), .e(convert_bcd_1_e),
    .d(convert_bcd_1_d), .c(convert_bcd_1_c));  // open: dp
  _7_Segment_Display #(.active("false")) u_7_segment_display_2 (
    .g(convert_bcd_2_g), .f(convert_bcd_2_f), .a(convert_bcd_2_a), .b(convert_bcd_2_b), .e(convert_bcd_2_e),
    .d(convert_bcd_2_d), .c(convert_bcd_2_c));  // open: dp
  convert_bcd convert_bcd_3 (
    .D3(t_ff_23_q), .D2(t_ff_20_q), .D1(t_ff_17_q), .D0(t_ff_11_q), .a(convert_bcd_3_a), .b(convert_bcd_3_b),
    .c(convert_bcd_3_c), .d(convert_bcd_3_d), .e(convert_bcd_3_e), .f(convert_bcd_3_f), .g(convert_bcd_3_g));
  convert_bcd convert_bcd_4 (
    .D3(1'b0), .D2(t_ff_24_q), .D1(t_ff_19_q), .D0(t_ff_12_q), .a(convert_bcd_4_a), .b(convert_bcd_4_b),
    .c(convert_bcd_4_c), .d(convert_bcd_4_d), .e(convert_bcd_4_e), .f(convert_bcd_4_f), .g(convert_bcd_4_g));
  _7_Segment_Display #(.active("false")) u_7_segment_display_3 (
    .g(convert_bcd_3_g), .f(convert_bcd_3_f), .a(convert_bcd_3_a), .b(convert_bcd_3_b), .e(convert_bcd_3_e),
    .d(convert_bcd_3_d), .c(convert_bcd_3_c));  // open: dp
  _7_Segment_Display #(.active("false")) u_7_segment_display_4 (
    .g(convert_bcd_4_g), .f(convert_bcd_4_f), .a(convert_bcd_4_a), .b(convert_bcd_4_b), .e(convert_bcd_4_e),
    .d(convert_bcd_4_d), .c(convert_bcd_4_c));  // open: dp
endmodule

module switch (
  input  in_1,
  input  in_2,
  input  in_3,
  output out_4
);

  wire and_1_out, and_2_out, not_1_out;

  not not_1 (not_1_out, in_2);
  and and_1 (and_1_out, in_1, not_1_out);
  and and_2 (and_2_out, in_2, in_3);
  or or_1 (out_4, and_1_out, and_2_out);
endmodule

module _7_bit_adder (
  input  T3,
  input  T3_2,
  input  T2,
  input  T2_2,
  input  T1,
  input  in_6,
  input  T3_3,
  input  T3_4,
  input  T2_3,
  input  T2_4,
  input  T1_2,
  input  T1_3,
  input  T0,
  input  T0_2,
  output S0,
  output S3,
  output S2,
  output S1,
  output S3_2,
  output S2_2,
  output S1_2
);

  wire adder_2_cout, adder_3_cout, adder_4_cout, adder_5_cout, adder_6_cout, adder_7_cout, xor_1_out,
       xor_2_out, xor_3_out, xor_4_out, xor_5_out, xor_6_out, xor_7_out;

  xor xor_1 (xor_1_out, T3, 1'b0);
  Adder #(.width(1)) adder_1 (.a(T3_2), .b(xor_1_out), .out(S3), .cin(adder_2_cout));  // open: cout
  xor xor_2 (xor_2_out, T2, 1'b0);
  Adder #(.width(1)) adder_2 (.a(T2_2), .b(xor_2_out), .out(S2), .cin(adder_3_cout), .cout(adder_2_cout));
  xor xor_3 (xor_3_out, T1, 1'b0);
  Adder #(.width(1)) adder_3 (.a(in_6), .b(xor_3_out), .out(S1), .cin(adder_4_cout), .cout(adder_3_cout));
  xor xor_4 (xor_4_out, T3_3, 1'b0);
  Adder #(.width(1)) adder_4 (.a(T3_4), .b(xor_4_out), .out(S3_2), .cin(adder_5_cout), .cout(adder_4_cout));
  xor xor_5 (xor_5_out, T2_3, 1'b0);
  Adder #(.width(1)) adder_5 (.a(T2_4), .b(xor_5_out), .out(S2_2), .cin(adder_6_cout), .cout(adder_5_cout));
  xor xor_6 (xor_6_out, T1_2, 1'b0);
  Adder #(.width(1)) adder_6 (.a(T1_3), .b(xor_6_out), .out(S1_2), .cin(adder_7_cout), .cout(adder_6_cout));
  xor xor_7 (xor_7_out, T0, 1'b0);
  Adder #(.width(1)) adder_7 (.a(T0_2), .b(xor_7_out), .out(S0), .cin(1'b0), .cout(adder_7_cout));
endmodule

module t_ff_updown (
  input  in_1
);

  wire and_1_out, and_2_out, and_3_out, and_4_out, and_5_out, and_6_out, and_7_out, and_8_out, and_9_out,
       and_10_out, clock_1_out, complete_turn_out, convert_bcd_1_a, convert_bcd_1_b, convert_bcd_1_c,
       convert_bcd_1_d, convert_bcd_1_e, convert_bcd_1_f, convert_bcd_1_g, convert_bcd_2_a, convert_bcd_2_b,
       convert_bcd_2_c, convert_bcd_2_d, convert_bcd_2_e, convert_bcd_2_f, convert_bcd_2_g, convert_bcd_3_a,
       convert_bcd_3_b, convert_bcd_3_c, convert_bcd_3_d, convert_bcd_3_e, convert_bcd_3_f, convert_bcd_3_g,
       convert_bcd_4_a, convert_bcd_4_b, convert_bcd_4_c, convert_bcd_4_d, convert_bcd_4_e, convert_bcd_4_f,
       convert_bcd_4_g, convert_bcd_5_a, convert_bcd_5_b, convert_bcd_5_c, convert_bcd_5_d, convert_bcd_5_e,
       convert_bcd_5_f, convert_bcd_5_g, mod6_op_1_carry, mod6_op_1_q1, mod6_op_1_q2, mod6_op_1_q3,
       not_1_out, or_1_out, or_2_out, or_3_out, or_4_out, or_5_out, pull_resistor_1_node, RESET, start_out,
       t_ff_1_q, t_ff_1_qn, t_ff_2_q, t_ff_2_qn, t_ff_3_q, t_ff_4_q, t_ff_4_qn, t_ff_5_q, t_ff_5_qn,
       t_ff_6_q, t_ff_7_q, t_ff_8_q, t_ff_9_q, t_ff_10_q, t_ff_11_q, t_ff_12_q, t_ff_13_q, t_ff_14_q,
       t_ff_15_q;

  Button complete_turn (.out(complete_turn_out));
  Button start (.out(start_out));
  Button u_RESET (.out(RESET));
  or or_1 (or_1_out, complete_turn_out, start_out);
  not not_1 (not_1_out, and_8_out);
  T_Flip_Flop t_ff_1 (
    .clk(pull_resistor_1_node), .T(1'b1), .Q(t_ff_1_q), .Qn(t_ff_1_qn), .reset(RESET));  // open: preset, en
  T_Flip_Flop t_ff_2 (.clk(not_1_out), .T(1'b1), .Q(t_ff_2_q), .Qn(t_ff_2_qn), .reset(RESET));  // open: preset, en
  T_Flip_Flop t_ff_3 (.clk(or_1_out), .T(or_1_out), .Q(t_ff_3_q));  // open: Qn, preset, reset, en
  T_Flip_Flop t_ff_4 (.clk(and_7_out), .T(1'b1), .Q(t_ff_4_q), .Qn(t_ff_4_qn));  // open: preset, reset, en
  T_Flip_Flop t_ff_5 (.clk(and_9_out), .T(1'b1), .Q(t_ff_5_q), .Qn(t_ff_5_qn));  // open: preset, reset, en
  Clock clock_1 (.out(clock_1_out));
  Pull_Resistor pull_resistor_1 (.node(pull_resistor_1_node));
  Transistor #(.\type ("n")) transistor_1 (.in(clock_1_out), .out(pull_resistor_1_node), .gate(t_ff_3_q));
  T_Flip_Flop t_ff_6 (
    .clk(pull_resistor_1_node), .T(t_ff_1_qn), .Q(t_ff_6_q), .reset(or_2_out));  // open: Qn, preset, en
  or or_2 (or_2_out, RESET, and_7_out);
  T_Flip_Flop t_ff_7 (.clk(and_7_out), .T(t_ff_4_qn), .Q(t_ff_7_q), .reset(and_8_out));  // open: Qn, preset, en
  T_Flip_Flop t_ff_8 (.clk(not_1_out), .T(t_ff_2_qn), .Q(t_ff_8_q), .reset(or_3_out));  // open: Qn, preset, en
  or or_3 (or_3_out, RESET, and_9_out);
  T_Flip_Flop t_ff_9 (.clk(and_9_out), .T(t_ff_5_qn), .Q(t_ff_9_q), .reset(and_10_out));  // open: Qn, preset, en
  and and_1 (and_1_out, ~t_ff_1_q, ~t_ff_6_q);  // AND_Gate
  or or_4 (or_4_out, RESET, and_7_out);
  and and_2 (and_2_out, ~t_ff_7_q, ~t_ff_4_q);  // AND_Gate
  and and_3 (and_3_out, ~t_ff_2_q, ~t_ff_8_q);  // AND_Gate
  or or_5 (or_5_out, RESET, and_9_out);
  and and_4 (and_4_out, ~t_ff_5_q, ~t_ff_9_q);  // AND_Gate
  T_Flip_Flop t_ff_10 (
    .clk(pull_resistor_1_node), .T(and_1_out), .Q(t_ff_10_q), .reset(or_4_out));  // open: Qn, preset, en
  T_Flip_Flop t_ff_11 (.clk(not_1_out), .T(and_3_out), .Q(t_ff_11_q), .reset(or_5_out));  // open: Qn, preset, en
  and and_5 (and_5_out, ~t_ff_1_q, ~t_ff_6_q, ~t_ff_10_q);  // AND_Gate
  T_Flip_Flop t_ff_12 (
    .clk(pull_resistor_1_node), .T(and_5_out), .Q(t_ff_12_q), .reset(RESET));  // open: Qn, preset, en
  T_Flip_Flop t_ff_13 (.clk(and_7_out), .T(and_2_out), .Q(t_ff_13_q));  // open: Qn, preset, reset, en
  and and_6 (and_6_out, ~t_ff_2_q, ~t_ff_8_q, ~t_ff_11_q);  // AND_Gate
  T_Flip_Flop t_ff_14 (.clk(not_1_out), .T(and_6_out), .Q(t_ff_14_q), .reset(RESET));  // open: Qn, preset, en
  T_Flip_Flop t_ff_15 (.clk(and_9_out), .T(and_4_out), .Q(t_ff_15_q));  // open: Qn, preset, reset, en
  and and_7 (and_7_out, t_ff_6_q, t_ff_12_q);
  and and_8 (and_8_out, t_ff_13_q, t_ff_7_q);
  and and_9 (and_9_out, t_ff_8_q, t_ff_14_q);
  and and_10 (and_10_out, ~t_ff_15_q, ~t_ff_9_q);  // AND_Gate
  mod6_op mod6_op_1 (
    .a(1'b0), .b(t_ff_15_q), .c(t_ff_9_q), .q1(mod6_op_1_q1), .q2(mod6_op_1_q2), .q3(mod6_op_1_q3),
    .carry(mod6_op_1_carry));
  convert_bcd convert_bcd_1 (
    .D3(t_ff_12_q), .D2(t_ff_10_q), .D1(t_ff_6_q), .D0(t_ff_1_q), .a(convert_bcd_1_a), .b(convert_bcd_1_b),
    .c(convert_bcd_1_c), .d(convert_bcd_1_d), .e(convert_bcd_1_e), .f(convert_bcd_1_f), .g(convert_bcd_1_g));
  convert_bcd convert_bcd_2 (
    .D3(1'b0), .D2(t_ff_13_q), .D1(t_ff_7_q), .D0(t_ff_4_q), .a(convert_bcd_2_a), .b(convert_bcd_2_b),
    .c(convert_bcd_2_c), .d(convert_bcd_2_d), .e(convert_bcd_2_e), .f(convert_bcd_2_f), .g(convert_bcd_2_g));
  convert_bcd convert_bcd_3 (
    .D3(t_ff_14_q), .D2(t_ff_11_q), .D1(t_ff_8_q), .D0(t_ff_2_q), .a(convert_bcd_3_a), .b(convert_bcd_3_b),
    .c(convert_bcd_3_c), .d(convert_bcd_3_d), .e(convert_bcd_3_e), .f(convert_bcd_3_f), .g(convert_bcd_3_g));
  convert_bcd convert_bcd_4 (
    .D3(1'b0), .D2(t_ff_15_q), .D1(t_ff_9_q), .D0(t_ff_5_q), .a(convert_bcd_4_a), .b(convert_bcd_4_b),
    .c(convert_bcd_4_c), .d(convert_bcd_4_d), .e(convert_bcd_4_e), .f(convert_bcd_4_f), .g(convert_bcd_4_g));
  _7_Segment_Display #(.active("false")) u_7_segment_display_1 (
    .g(convert_bcd_1_g), .f(convert_bcd_1_f), .a(convert_bcd_1_a), .b(convert_bcd_1_b), .e(convert_bcd_1_e),
    .d(convert_bcd_1_d), .c(convert_bcd_1_c));  // open: dp
  _7_Segment_Display #(.active("false")) u_7_segment_display_2 (
    .g(convert_bcd_2_g), .f(convert_bcd_2_f), .a(convert_bcd_2_a), .b(convert_bcd_2_b), .e(convert_bcd_2_e),
    .d(convert_bcd_2_d), .c(convert_bcd_2_c));  // open: dp
  _7_Segment_Display #(.active("false")) u_7_segment_display_3 (
    .g(convert_bcd_3_g), .f(convert_bcd_3_f), .a(convert_bcd_3_a), .b(convert_bcd_3_b), .e(convert_bcd_3_e),
    .d(convert_bcd_3_d), .c(convert_bcd_3_c));  // open: dp
  convert_bcd convert_bcd_5 (
    .D3(mod6_op_1_q1), .D2(mod6_op_1_q2), .D1(mod6_op_1_q3), .D0(mod6_op_1_carry), .a(convert_bcd_5_a),
    .b(convert_bcd_5_b), .c(convert_bcd_5_c), .d(convert_bcd_5_d), .e(convert_bcd_5_e), .f(convert_bcd_5_f),
    .g(convert_bcd_5_g));
  _7_Segment_Display #(.active("false")) u_7_segment_display_4 (
    .g(convert_bcd_4_g), .f(convert_bcd_4_f), .a(convert_bcd_4_a), .b(convert_bcd_4_b), .e(convert_bcd_4_e),
    .d(convert_bcd_4_d), .c(convert_bcd_4_c));  // open: dp
  _7_Segment_Display #(.active("false")) u_7_segment_display_5 (
    .g(convert_bcd_5_g), .f(convert_bcd_5_f), .a(convert_bcd_5_a), .b(convert_bcd_5_b), .e(convert_bcd_5_e),
    .d(convert_bcd_5_d), .c(convert_bcd_5_c));  // open: dp
endmodule

module _3_bit_adder (
  input  T2,
  input  T2_2,
  input  T1,
  input  T1_2,
  input  T0,
  input  T0_2,
  output out_7,
  output out_8,
  output out_9
);

  wire adder_1_out, adder_2_cout, adder_2_out, adder_3_cout, adder_3_out, xor_1_out, xor_2_out, xor_3_out;

  xor xor_1 (xor_1_out, T2, 1'b0);
  Adder #(.width(1)) adder_1 (.a(T2_2), .b(xor_1_out), .out(adder_1_out), .cin(adder_2_cout));  // open: cout
  xor xor_2 (xor_2_out, T1, 1'b0);
  Adder #(.width(1)) adder_2 (.a(T1_2), .b(xor_2_out), .out(adder_2_out), .cin(adder_3_cout), .cout(adder_2_cout));
  xor xor_3 (xor_3_out, T0, 1'b0);
  Adder #(.width(1)) adder_3 (.a(T0_2), .b(xor_3_out), .out(adder_3_out), .cin(1'b0), .cout(adder_3_cout));
  // AND_Gate and_1 is placed but not wired
  nand nand_1 (out_7, ~adder_3_out, adder_2_out, adder_1_out);  // NAND_Gate

  assign out_8 = out_7;
  assign out_9 = out_7;
endmodule

module mod6_op (
  input  a,
  input  b,
  input  c,
  output q1,
  output q2,
  output q3,
  output carry
);

  wire and_1_out, and_2_out, and_3_out, and_4_out, and_5_out, and_6_out, and_7_out, not_1_out, not_2_out,
       not_3_out, not_4_out, not_5_out, not_6_out;

  not not_1 (not_1_out, a);
  not not_2 (not_2_out, b);
  not not_3 (not_3_out, c);
  not not_4 (not_4_out, a);
  not not_5 (not_5_out, b);
  not not_6 (not_6_out, c);
  not not_7 (q3, c);
  and and_1 (and_1_out, b, c);
  and and_2 (and_2_out, not_1_out, not_2_out, c);
  and and_3 (and_3_out, b, not_3_out);
  and and_4 (and_4_out, a, b);
  and and_5 (and_5_out, not_4_out, not_5_out, not_6_out);
  and and_6 (and_6_out, a, c);
  and and_7 (and_7_out, a, b);
  or or_1 (carry, and_1_out, a);
  or or_2 (q1, and_2_out, and_3_out, and_4_out);
  or or_3 (q2, and_5_out, and_6_out, and_7_out);
endmodule

module updateS_R (
  input  a,
  input  select,
  output set,
  output reset
);

  wire not_1_out;

  and and_1 (set, a, select);
  not not_1 (not_1_out, a);
  and and_2 (reset, not_1_out, select);
endmodule

module test1 (
);

  wire and_1_out, and_2_out, and_3_out, and_4_out, and_5_out, and_6_out, and_7_out, clock_1_out, clock_2_out,
       comp_out, convert_bcd_1_a, convert_bcd_1_b, convert_bcd_1_c, convert_bcd_1_d, convert_bcd_1_e,
       convert_bcd_1_f, convert_bcd_1_g, d_ff_1_q, d_ff_2_q, d_ff_3_q, d_ff_3_qn, d_ff_4_q, d_ff_5_q,
       mod6_op_1_p5, mod6_op_1_p6, mod6_op_1_p7, multiplexer_1_out, multiplexer_2_out, multiplexer_3_out,
       not_1_out, or_1_out, or_2_out, or_3_out, or_4_out, start_out, t_ff_1_q, t_ff_2_q, transistor_1_out;

  Button comp (.out(comp_out));
  Button start (.out(start_out));
  and and_1 (and_1_out, t_ff_1_q, not_1_out);
  or or_1 (or_1_out, comp_out, start_out);
  T_Flip_Flop t_ff_1 (.clk(comp_out), .T(comp_out), .Q(t_ff_1_q));  // open: Qn, preset, reset, en
  D_Flip_Flop d_ff_1 (.clk(and_1_out), .D(1'b1), .Q(d_ff_1_q), .reset(d_ff_2_q));  // open: Qn, preset, en
  Clock clock_1 (.out(clock_1_out));
  Clock clock_2 (.out(clock_2_out));
  T_Flip_Flop t_ff_2 (.clk(or_1_out), .T(or_1_out), .Q(t_ff_2_q));  // open: Qn, preset, reset, en
  Transistor #(.\type ("n")) transistor_1 (.in(clock_2_out), .out(transistor_1_out), .gate(t_ff_2_q));
  or or_2 (or_2_out, d_ff_2_q, transistor_1_out);
  not not_1 (not_1_out, transistor_1_out);
  D_Flip_Flop d_ff_2 (.clk(clock_1_out), .D(d_ff_1_q), .Q(d_ff_2_q));  // open: Qn, preset, en, reset
  Pull_Resistor pull_resistor_1 (.node(transistor_1_out));
  Multiplexer multiplexer_1 (.in0(d_ff_3_qn), .in1(mod6_op_1_p7), .out(multiplexer_1_out), .sel(t_ff_1_q));  // open: en
  D_Flip_Flop d_ff_3 (.clk(or_2_out), .D(multiplexer_1_out), .Q(d_ff_3_q), .Qn(d_ff_3_qn));  // open: preset, en, reset
  Multiplexer multiplexer_2 (.in0(or_3_out), .in1(mod6_op_1_p6), .out(multiplexer_2_out), .sel(t_ff_1_q));  // open: en
  D_Flip_Flop d_ff_4 (.clk(or_2_out), .D(multiplexer_2_out), .Q(d_ff_4_q), .reset(and_7_out));  // open: Qn, preset, en
  and and_2 (and_2_out, ~d_ff_4_q, ~d_ff_3_q);  // AND_Gate
  or or_3 (or_3_out, and_2_out, and_3_out);
  and and_3 (and_3_out, d_ff_4_q, d_ff_3_q);
  Multiplexer multiplexer_3 (.in0(or_4_out), .in1(mod6_op_1_p5), .out(multiplexer_3_out), .sel(t_ff_1_q));  // open: en
  D_Flip_Flop d_ff_5 (.clk(or_2_out), .D(multiplexer_3_out), .Q(d_ff_5_q));  // open: Qn, preset, en, reset
  and and_4 (and_4_out, ~d_ff_5_q, ~d_ff_4_q, ~d_ff_3_q);  // AND_Gate
  and and_5 (and_5_out, d_ff_5_q, d_ff_4_q);
  and and_6 (and_6_out, d_ff_5_q, d_ff_3_q);
  and and_7 (and_7_out, d_ff_5_q, d_ff_4_q);
  or or_4 (or_4_out, and_4_out, and_5_out, and_6_out);
  convert_bcd convert_bcd_1 (
    .D3(1'b0), .D2(d_ff_5_q), .D1(d_ff_4_q), .D0(d_ff_3_q), .a(convert_bcd_1_a), .b(convert_bcd_1_b),
    .c(convert_bcd_1_c), .d(convert_bcd_1_d), .e(convert_bcd_1_e), .f(convert_bcd_1_f), .g(convert_bcd_1_g));
  // mod6_op mod6_op_1: pin names not known; wires that end beside it: 1'b0, d_ff_5_q, d_ff_4_q, d_ff_3_q, mod6_op_1_p5, mod6_op_1_p6, mod6_op_1_p7
  _7_Segment_Display #(.active("false")) u_7_segment_display_1 (
    .g(convert_bcd_1_g), .f(convert_bcd_1_f), .a(convert_bcd_1_a), .b(convert_bcd_1_b), .e(convert_bcd_1_e),
    .d(convert_bcd_1_d), .c(convert_bcd_1_c));  // open: dp
endmodule

module choose_sig (
  input  plus,
  input  sig,
  input  ori,
  output set
);

  wire and_1_out, and_2_out, not_1_out;

  not not_1 (not_1_out, plus);
  and and_1 (and_1_out, not_1_out, ori);
  and and_2 (and_2_out, plus, sig);
  or or_1 (set, and_1_out, and_2_out);
endmodule

module d_ff_updown (
  input  complete_turn,
  input  start,
  input  RESET,
  output a2_hr,
  output b2_hr,
  output c2_hr,
  output d2_hr,
  output e2_hr,
  output f2_hr,
  output g2_hr,
  output a2_min1,
  output b2_min1,
  output c2_min1,
  output d2_min1,
  output e2_min1,
  output f2_min1,
  output g2_min1,
  output a2_min,
  output b2_min,
  output c2_min,
  output d2_min,
  output e2_min,
  output f2_min,
  output g2_min,
  output a2_sec1,
  output b2_sec1,
  output c2_sec1,
  output d2_sec1,
  output e2_sec1,
  output f2_sec1,
  output g2_sec1,
  output a2_sec,
  output b2_sec,
  output c2_sec,
  output d2_sec,
  output e2_sec,
  output f2_sec,
  output g2_sec,
  output a_hr,
  output b_hr,
  output c_hr,
  output d_hr,
  output e_hr,
  output f_hr,
  output g_hr,
  output a_min1,
  output b_min1,
  output c_min1,
  output d_min1,
  output e_min1,
  output f_min1,
  output g_min1,
  output a_min,
  output b_min,
  output c_min,
  output d_min,
  output e_min,
  output f_min,
  output g_min,
  output a_sec1,
  output b_sec1,
  output c_sec1,
  output d_sec1,
  output e_sec1,
  output f_sec1,
  output g_sec1,
  output a_sec,
  output b_sec,
  output c_sec,
  output d_sec,
  output e_sec,
  output f_sec,
  output g_sec
);

  wire and_1_out, and_2_out, and_3_out, and_4_out, and_5_out, and_6_out, and_7_out, and_8_out, and_9_out,
       and_10_out, and_11_out, and_12_out, and_13_out, and_14_out, and_15_out, and_16_out, and_17_out,
       and_18_out, and_19_out, and_20_out, and_21_out, and_22_out, and_23_out, and_24_out, and_25_out,
       and_26_out, and_27_out, and_28_out, and_29_out, and_30_out, and_31_out, and_32_out, and_33_out,
       and_34_out, and_35_out, and_36_out, and_37_out, and_38_out, and_39_out, and_40_out, and_41_out,
       and_42_out, and_43_out, and_44_out, and_45_out, and_46_out, and_47_out, and_49_out, and_50_out,
       and_52_out, and_53_out, and_54_out, and_55_out, and_56_out, and_57_out, and_58_out, and_59_out,
       and_60_out, and_61_out, and_62_out, and_63_out, and_65_out, and_66_out, and_67_out, and_68_out,
       and_69_out, and_70_out, and_72_out, and_73_out, and_74_out, and_75_out, and_76_out, and_77_out,
       and_78_out, and_79_out, carry, carry_prime, clock_1_out, clock_2_out, clock_3_out, clock_4_out,
       clock_5_out, clock_6_out, comp, d_ff_1_q, d_ff_2_q, d_ff_3_q, d_ff_4_q, d_ff_5_q, d_ff_6_q, d_ff_7_q,
       d_ff_8_q, d_ff_9_qn, d_ff_10_q, d_ff_11_qn, d_ff_12_q, d_ff_13_qn, d_ff_14_qn, multiplexer_1_out,
       multiplexer_2_out, multiplexer_3_out, multiplexer_4_out, multiplexer_5_out, multiplexer_6_out,
       not_1_out, not_2_out, or_1_out, or_2_out, or_3_out, or_4_out, or_5_out, or_6_out, or_7_out, or_8_out,
       or_9_out, or_10_out, or_11_out, or_12_out, or_13_out, or_14_out, or_15_out, or_16_out, or_17_out,
       or_18_out, or_19_out, or_20_out, or_21_out, or_22_out, or_23_out, or_24_out, or_25_out, or_26_out,
       or_27_out, or_28_out, or_29_out, or_30_out, or_31_out, or_32_out, or_33_out, or_34_out, or_35_out,
       or_36_out, or_37_out, or_38_out, or_39_out, or_40_out, or_41_out, or_42_out, or_43_out, or_44_out,
       or_45_out, or_46_out, or_47_out, or_48_out, or_49_out, or_50_out, or_51_out, or_52_out, or_53_out,
       or_54_out, or_55_out, or_56_out, or_57_out, or_58_out, or_59_out, or_60_out, or_61_out, or_62_out,
       pull_resistor_1_node, pull_resistor_2_node, Q0, Q0_prime, Q1, Q1_prime, Q2, Q2_prime, Q3, Q3_prime,
       Q4, Q4_prime, Q4N, Q4N_prime, Q5, Q5_prime, Q5N, Q5N_prime, Q6, Q6_prime, Q6N, Q6N_prime, Q7,
       Q7_prime, Q8, Q8_prime, Q9, Q9_prime, Q10, Q10_prime, Q11, Q11_prime, Q12, Q12_prime, Q13, Q13_prime,
       Q14, Q14_prime, Q15, Q15_prime, Q16, Q16_prime, Q17, Q17_prime, t_ff_2_qn, t_ff_3_qn, t_ff_10_q, up,
       up_prime, update, update_prime;

  T_Flip_Flop t_ff_1 (.clk(complete_turn), .T(complete_turn), .Q(comp), .reset(RESET));  // open: Qn, preset, en
  and and_1 (and_1_out, RESET, ~t_ff_2_qn);  // AND_Gate
  not not_1 (not_1_out, comp);
  and and_2 (and_2_out, RESET, ~t_ff_3_qn);  // AND_Gate
  and and_3 (and_3_out, Q1, Q0);
  or or_1 (or_1_out, and_3_out, and_4_out, and_5_out);
  and and_4 (and_4_out, Q2, ~Q1, ~Q0);  // AND_Gate
  and and_5 (and_5_out, Q3, ~Q0);  // AND_Gate
  or or_2 (or_2_out, and_5_out, and_6_out, and_7_out);
  and and_6 (and_6_out, Q2, Q0);
  and and_7 (and_7_out, Q2, Q1);
  and and_8 (and_8_out, Q3, Q0);
  or or_3 (or_3_out, and_8_out, and_9_out);
  and and_9 (and_9_out, ~Q3, ~Q2, ~Q1, ~Q0);  // AND_Gate
  D_Flip_Flop d_ff_1 (.clk(comp), .D(1'b1), .Q(d_ff_1_q), .reset(d_ff_5_q));  // open: Qn, preset, en
  Clock clock_1 (.out(clock_1_out));
  D_Flip_Flop d_ff_2 (.clk(up), .D(1'b1), .Q(d_ff_2_q), .reset(d_ff_6_q));  // open: Qn, preset, en
  Clock clock_2 (.out(clock_2_out));
  T_Flip_Flop t_ff_2 (.clk(or_4_out), .T(or_4_out), .Qn(t_ff_2_qn));  // open: Q, preset, reset, en
  or or_4 (or_4_out, start, and_1_out);
  and and_10 (and_10_out, Q1_prime, Q0_prime);
  and and_11 (and_11_out, Q2_prime, ~Q1_prime, ~Q0_prime);  // AND_Gate
  or or_5 (or_5_out, and_10_out, and_11_out, and_12_out);
  and and_12 (and_12_out, Q3_prime, ~Q0_prime);  // AND_Gate
  or or_6 (or_6_out, and_12_out, and_13_out, and_14_out);
  and and_13 (and_13_out, Q2_prime, Q0_prime);
  and and_14 (and_14_out, Q2_prime, Q1_prime);
  and and_15 (and_15_out, Q3_prime, Q0_prime);
  or or_7 (or_7_out, and_15_out, and_16_out);
  and and_16 (and_16_out, ~Q3_prime, ~Q2_prime, ~Q1_prime, ~Q0_prime);  // AND_Gate
  D_Flip_Flop d_ff_3 (.clk(not_1_out), .D(1'b1), .Q(d_ff_3_q), .reset(d_ff_7_q));  // open: Qn, preset, en
  Clock clock_3 (.out(clock_3_out));
  D_Flip_Flop d_ff_4 (.clk(up_prime), .D(1'b1), .Q(d_ff_4_q), .reset(d_ff_8_q));  // open: Qn, preset, en
  Clock clock_4 (.out(clock_4_out));
  T_Flip_Flop t_ff_3 (.clk(or_8_out), .T(or_8_out), .Qn(t_ff_3_qn));  // open: Q, preset, reset, en
  or or_8 (or_8_out, start, and_2_out);
  D_Flip_Flop d_ff_5 (.clk(clock_1_out), .D(d_ff_1_q), .Q(d_ff_5_q));  // open: Qn, preset, en, reset
  D_Flip_Flop d_ff_6 (.clk(clock_2_out), .D(d_ff_2_q), .Q(d_ff_6_q), .reset(d_ff_10_q));  // open: Qn, preset, en
  D_Flip_Flop d_ff_7 (.clk(clock_3_out), .D(d_ff_3_q), .Q(d_ff_7_q));  // open: Qn, preset, en, reset
  not not_2 (not_2_out, comp);
  D_Flip_Flop d_ff_8 (.clk(clock_4_out), .D(d_ff_4_q), .Q(d_ff_8_q), .reset(d_ff_12_q));  // open: Qn, preset, en
  or or_9 (or_9_out, complete_turn, start);
  and and_17 (and_17_out, RESET, t_ff_10_q);
  or or_10 (or_10_out, and_54_out, and_18_out);
  T_Flip_Flop t_ff_4 (.clk(or_58_out), .T(1'b1), .Q(Q14), .reset(RESET));  // open: Qn, preset, en
  or or_11 (or_11_out, and_59_out, and_21_out);
  T_Flip_Flop t_ff_5 (.clk(or_60_out), .T(1'b1), .Q(Q14_prime), .reset(RESET));  // open: Qn, preset, en
  D_Flip_Flop d_ff_9 (
    .clk(pull_resistor_1_node), .D(d_ff_9_qn), .Q(Q0), .Qn(d_ff_9_qn), .reset(RESET));  // open: preset, en
  or or_12 (or_12_out, or_9_out, and_17_out);
  or or_13 (or_13_out, update, d_ff_5_q);
  Multiplexer multiplexer_1 (.in0(d_ff_13_qn), .in1(Q4N), .out(multiplexer_1_out), .sel(comp));  // open: en
  D_Flip_Flop d_ff_10 (.clk(clock_2_out), .D(d_ff_6_q), .Q(d_ff_10_q));  // open: Qn, preset, en, reset
  and and_18 (and_18_out, ~carry, d_ff_10_q);  // AND_Gate
  T_Flip_Flop t_ff_6 (.clk(or_10_out), .T(1'b1), .Q(Q7), .reset(RESET));  // open: Qn, preset, en
  T_Flip_Flop t_ff_7 (.clk(or_57_out), .T(1'b1), .Q(Q11), .reset(RESET));  // open: Qn, preset, en
  and and_19 (and_19_out, ~Q14, ~up);  // AND_Gate
  and and_20 (and_20_out, Q14, up);
  D_Flip_Flop d_ff_11 (
    .clk(pull_resistor_2_node), .D(d_ff_11_qn), .Q(Q0_prime), .Qn(d_ff_11_qn), .reset(RESET));  // open: preset, en
  or or_14 (or_14_out, update_prime, d_ff_7_q);
  Multiplexer multiplexer_2 (.in0(d_ff_14_qn), .in1(Q4N_prime), .out(multiplexer_2_out), .sel(not_2_out));  // open: en
  D_Flip_Flop d_ff_12 (.clk(clock_4_out), .D(d_ff_8_q), .Q(d_ff_12_q));  // open: Qn, preset, en, reset
  and and_21 (and_21_out, ~carry_prime, d_ff_12_q);  // AND_Gate
  T_Flip_Flop t_ff_8 (.clk(or_11_out), .T(1'b1), .Q(Q7_prime), .reset(RESET));  // open: Qn, preset, en
  T_Flip_Flop t_ff_9 (.clk(or_59_out), .T(1'b1), .Q(Q11_prime), .reset(RESET));  // open: Qn, preset, en
  and and_22 (and_22_out, ~Q14_prime, ~up_prime);  // AND_Gate
  and and_23 (and_23_out, Q14_prime, up_prime);
  Clock clock_5 (.out(clock_5_out));
  T_Flip_Flop t_ff_10 (.clk(or_12_out), .T(or_12_out), .Q(t_ff_10_q));  // open: Qn, preset, reset, en
  D_Flip_Flop d_ff_13 (
    .clk(or_13_out), .D(multiplexer_1_out), .Q(Q4), .Qn(d_ff_13_qn), .reset(RESET));  // open: preset, en
  and and_24 (and_24_out, ~Q7, ~up);  // AND_Gate
  and and_25 (and_25_out, Q7, up);
  and and_26 (and_26_out, ~Q11, ~up);  // AND_Gate
  and and_27 (and_27_out, Q11, up);
  or or_15 (or_15_out, and_19_out, and_20_out);
  or or_16 (or_16_out, t_ff_2_qn, RESET);
  Clock clock_6 (.out(clock_6_out));
  D_Flip_Flop d_ff_14 (
    .clk(or_14_out), .D(multiplexer_2_out), .Q(Q4_prime), .Qn(d_ff_14_qn), .reset(RESET));  // open: preset, en
  and and_28 (and_28_out, ~Q7_prime, ~up_prime);  // AND_Gate
  and and_29 (and_29_out, Q7_prime, up_prime);
  and and_30 (and_30_out, ~Q11_prime, ~up_prime);  // AND_Gate
  and and_31 (and_31_out, Q11_prime, up_prime);
  or or_17 (or_17_out, and_22_out, and_23_out);
  or or_18 (or_18_out, t_ff_3_qn, RESET);
  or or_19 (or_19_out, RESET, update);
  Pull_Resistor pull_resistor_1 (.node(pull_resistor_1_node));
  Transistor #(.\type ("n")) transistor_1 (.in(clock_5_out), .out(pull_resistor_1_node), .gate(t_ff_10_q));
  Multiplexer multiplexer_3 (.in0(or_43_out), .in1(Q5N), .out(multiplexer_3_out), .sel(comp));  // open: en
  or or_20 (or_20_out, and_24_out, and_25_out);
  T_Flip_Flop t_ff_11 (.clk(or_10_out), .T(or_20_out), .Q(Q8), .reset(or_21_out));  // open: Qn, preset, en
  or or_21 (or_21_out, RESET, and_69_out, and_68_out);
  or or_22 (or_22_out, and_26_out, and_27_out);
  T_Flip_Flop t_ff_12 (.clk(or_58_out), .T(or_15_out), .Q(Q15), .preset(or_16_out), .reset(or_23_out));  // open: Qn, en
  or or_23 (or_23_out, and_70_out, and_58_out);
  or or_24 (or_24_out, RESET, update_prime);
  Pull_Resistor pull_resistor_2 (.node(pull_resistor_2_node));
  Transistor #(.\type ("n")) transistor_2 (.in(clock_6_out), .out(pull_resistor_2_node), .gate(comp));
  Multiplexer multiplexer_4 (.in0(or_46_out), .in1(Q5N_prime), .out(multiplexer_4_out), .sel(not_2_out));  // open: en
  or or_25 (or_25_out, and_28_out, and_29_out);
  T_Flip_Flop t_ff_13 (.clk(or_11_out), .T(or_25_out), .Q(Q8_prime), .reset(or_26_out));  // open: Qn, preset, en
  or or_26 (or_26_out, RESET, and_75_out, and_76_out);
  or or_27 (or_27_out, and_30_out, and_31_out);
  T_Flip_Flop t_ff_14 (
    .clk(or_60_out), .T(or_17_out), .Q(Q15_prime), .preset(or_18_out), .reset(or_28_out));  // open: Qn, en
  or or_28 (or_28_out, and_77_out, and_63_out);
  D_Flip_Flop d_ff_15 (.clk(pull_resistor_1_node), .D(or_1_out), .Q(Q1), .reset(or_19_out));  // open: Qn, preset, en
  D_Flip_Flop d_ff_16 (.clk(or_13_out), .D(multiplexer_3_out), .Q(Q5), .reset(or_29_out));  // open: Qn, preset, en
  or or_29 (or_29_out, RESET, and_54_out);
  and and_32 (and_32_out, ~Q8, ~Q7, ~up);  // AND_Gate
  and and_33 (and_33_out, Q8, Q7, up);
  T_Flip_Flop t_ff_15 (.clk(or_57_out), .T(or_22_out), .Q(Q12), .reset(or_30_out));  // open: Qn, preset, en
  or or_30 (or_30_out, and_78_out, RESET, and_57_out);
  and and_34 (and_34_out, ~Q15, ~Q14, ~up);  // AND_Gate
  or or_31 (or_31_out, and_34_out, and_35_out);
  and and_35 (and_35_out, Q15, Q14, up);
  or or_32 (or_32_out, RESET, and_58_out);
  D_Flip_Flop d_ff_17 (
    .clk(pull_resistor_2_node), .D(or_5_out), .Q(Q1_prime), .reset(or_24_out));  // open: Qn, preset, en
  D_Flip_Flop d_ff_18 (
    .clk(or_14_out), .D(multiplexer_4_out), .Q(Q5_prime), .reset(or_33_out));  // open: Qn, preset, en
  or or_33 (or_33_out, RESET, and_59_out);
  and and_36 (and_36_out, ~Q8_prime, ~Q7_prime, ~up_prime);  // AND_Gate
  and and_37 (and_37_out, Q8_prime, Q7_prime, up_prime);
  T_Flip_Flop t_ff_16 (.clk(or_59_out), .T(or_27_out), .Q(Q12_prime), .reset(or_34_out));  // open: Qn, preset, en
  or or_34 (or_34_out, and_79_out, RESET, and_62_out);
  and and_38 (and_38_out, ~Q15_prime, ~Q14_prime, ~up_prime);  // AND_Gate
  or or_35 (or_35_out, and_38_out, and_39_out);
  and and_39 (and_39_out, Q15_prime, Q14_prime, up_prime);
  or or_36 (or_36_out, RESET, and_63_out);
  D_Flip_Flop d_ff_19 (.clk(pull_resistor_1_node), .D(or_2_out), .Q(Q2), .reset(or_37_out));  // open: Qn, preset, en
  or or_37 (or_37_out, RESET, update);
  and and_40 (and_40_out, ~Q4, ~Q5);  // AND_Gate
  and and_41 (and_41_out, Q4, Q5);
  or or_38 (or_38_out, and_32_out, and_33_out);
  T_Flip_Flop t_ff_17 (.clk(or_10_out), .T(or_38_out), .Q(Q9), .reset(or_39_out));  // open: Qn, preset, en
  or or_39 (or_39_out, RESET, and_68_out);
  and and_42 (and_42_out, ~Q12, ~Q11, ~up);  // AND_Gate
  and and_43 (and_43_out, Q12, Q11, up);
  T_Flip_Flop t_ff_18 (.clk(or_58_out), .T(or_31_out), .Q(Q16), .reset(or_32_out));  // open: Qn, preset, en
  D_Flip_Flop d_ff_20 (
    .clk(pull_resistor_2_node), .D(or_6_out), .Q(Q2_prime), .reset(or_40_out));  // open: Qn, preset, en
  or or_40 (or_40_out, RESET, update_prime);
  and and_44 (and_44_out, ~Q4_prime, ~Q5_prime);  // AND_Gate
  and and_45 (and_45_out, Q4_prime, Q5_prime);
  or or_41 (or_41_out, and_36_out, and_37_out);
  T_Flip_Flop t_ff_19 (.clk(or_11_out), .T(or_41_out), .Q(Q9_prime), .reset(or_42_out));  // open: Qn, preset, en
  or or_42 (or_42_out, RESET, and_76_out);
  and and_46 (and_46_out, ~Q12_prime, ~Q11_prime, ~up_prime);  // AND_Gate
  and and_47 (and_47_out, Q12_prime, Q11_prime, up_prime);
  T_Flip_Flop t_ff_20 (.clk(or_60_out), .T(or_35_out), .Q(Q16_prime), .reset(or_36_out));  // open: Qn, preset, en
  or or_43 (or_43_out, and_40_out, and_41_out);
  Multiplexer multiplexer_5 (.in0(or_61_out), .in1(Q6N), .out(multiplexer_5_out), .sel(comp));  // open: en
  and and_48 (up, comp, ~carry);  // AND_Gate
  or or_44 (or_44_out, and_42_out, and_43_out);
  and and_49 (and_49_out, ~Q14, ~Q15, ~Q16, ~up);  // AND_Gate
  and and_50 (and_50_out, Q14, Q15, Q16, up);
  T_Flip_Flop t_ff_21 (.clk(or_58_out), .T(or_52_out), .Q(Q17), .reset(or_45_out));  // open: Qn, preset, en
  or or_45 (or_45_out, RESET, and_58_out, and_70_out);
  or or_46 (or_46_out, and_44_out, and_45_out);
  Multiplexer multiplexer_6 (.in0(or_62_out), .in1(Q6N_prime), .out(multiplexer_6_out), .sel(not_2_out));  // open: en
  and and_51 (up_prime, ~comp, ~carry_prime);  // AND_Gate
  or or_47 (or_47_out, and_46_out, and_47_out);
  and and_52 (and_52_out, ~Q14_prime, ~Q15_prime, ~Q16_prime, ~up_prime);  // AND_Gate
  and and_53 (and_53_out, Q14_prime, Q15_prime, Q16_prime, up_prime);
  T_Flip_Flop t_ff_22 (.clk(or_60_out), .T(or_56_out), .Q(Q17_prime), .reset(or_48_out));  // open: Qn, preset, en
  or or_48 (or_48_out, RESET, and_63_out, and_77_out);
  D_Flip_Flop d_ff_21 (.clk(pull_resistor_1_node), .D(or_3_out), .Q(Q3), .reset(RESET));  // open: Qn, preset, en
  D_Flip_Flop d_ff_22 (.clk(or_13_out), .D(multiplexer_5_out), .Q(Q6), .reset(RESET));  // open: Qn, preset, en
  and and_54 (and_54_out, Q6, Q5);
  and and_55 (and_55_out, ~Q7, ~Q8, ~Q9, ~up);  // AND_Gate
  or or_49 (or_49_out, and_55_out, and_56_out);
  and and_56 (and_56_out, Q7, Q8, Q9, up);
  T_Flip_Flop t_ff_23 (.clk(or_10_out), .T(or_49_out), .Q(Q10), .reset(or_50_out));  // open: Qn, preset, en
  or or_50 (or_50_out, RESET, and_69_out);
  T_Flip_Flop t_ff_24 (.clk(or_57_out), .T(or_44_out), .Q(Q13), .reset(or_51_out));  // open: Qn, preset, en
  or or_51 (or_51_out, RESET, and_78_out);
  and and_57 (and_57_out, Q12, ~up, Q13);  // AND_Gate
  or or_52 (or_52_out, and_49_out, and_50_out);
  and and_58 (and_58_out, Q15, ~up, Q17);  // AND_Gate
  D_Flip_Flop d_ff_23 (.clk(pull_resistor_2_node), .D(or_7_out), .Q(Q3_prime), .reset(RESET));  // open: Qn, preset, en
  D_Flip_Flop d_ff_24 (.clk(or_14_out), .D(multiplexer_6_out), .Q(Q6_prime), .reset(RESET));  // open: Qn, preset, en
  and and_59 (and_59_out, Q6_prime, Q5_prime);
  and and_60 (and_60_out, ~Q7_prime, ~Q8_prime, ~Q9_prime, ~up_prime);  // AND_Gate
  or or_53 (or_53_out, and_60_out, and_61_out);
  and and_61 (and_61_out, Q7_prime, Q8_prime, Q9_prime, up_prime);
  T_Flip_Flop t_ff_25 (.clk(or_11_out), .T(or_53_out), .Q(Q10_prime), .reset(or_54_out));  // open: Qn, preset, en
  or or_54 (or_54_out, RESET, and_75_out);
  T_Flip_Flop t_ff_26 (.clk(or_59_out), .T(or_47_out), .Q(Q13_prime), .reset(or_55_out));  // open: Qn, preset, en
  or or_55 (or_55_out, RESET, and_79_out);
  and and_62 (and_62_out, Q12_prime, ~up_prime, Q13_prime);  // AND_Gate
  or or_56 (or_56_out, and_52_out, and_53_out);
  and and_63 (and_63_out, Q15_prime, ~up_prime, Q17_prime);  // AND_Gate
  and and_64 (update, Q0, Q3);
  and and_65 (and_65_out, ~Q6, ~Q4, ~Q5);  // AND_Gate
  and and_66 (and_66_out, Q6, Q4);
  and and_67 (and_67_out, Q6, Q5);
  mod6_op mod6_op_1 (.a(Q6), .b(Q5), .c(Q4), .q1(Q6N), .q2(Q5N), .q3(Q4N), .carry(carry));
  and and_68 (and_68_out, Q8, ~up, Q10);  // AND_Gate
  and and_69 (and_69_out, Q8, up, Q10);
  or or_57 (or_57_out, and_68_out, and_69_out);
  or or_58 (or_58_out, and_57_out, and_78_out);
  and and_70 (and_70_out, Q15, up, Q17);
  and and_71 (update_prime, Q0_prime, Q3_prime);
  and and_72 (and_72_out, ~Q6_prime, ~Q4_prime, ~Q5_prime);  // AND_Gate
  and and_73 (and_73_out, Q6_prime, Q4_prime);
  and and_74 (and_74_out, Q6_prime, Q5_prime);
  mod6_op mod6_op_2 (
    .a(Q6_prime), .b(Q5_prime), .c(Q4_prime), .q1(Q6N_prime), .q2(Q5N_prime), .q3(Q4N_prime),
    .carry(carry_prime));
  and and_75 (and_75_out, Q8_prime, up_prime, Q10_prime);
  and and_76 (and_76_out, Q8_prime, ~up_prime, Q10_prime);  // AND_Gate
  or or_59 (or_59_out, and_76_out, and_75_out);
  or or_60 (or_60_out, and_62_out, and_79_out);
  and and_77 (and_77_out, Q15_prime, up_prime, Q17_prime);
  or or_61 (or_61_out, and_65_out, and_66_out, and_67_out);
  and and_78 (and_78_out, Q12, up, Q13);
  or or_62 (or_62_out, and_72_out, and_73_out, and_74_out);
  and and_79 (and_79_out, Q12_prime, up_prime, Q13_prime);
  convert_bcd convert_bcd_1 (
    .D3(Q17_prime), .D2(Q16_prime), .D1(Q15_prime), .D0(Q14_prime), .a(a2_hr), .b(b2_hr), .c(c2_hr),
    .d(d2_hr), .e(e2_hr), .f(f2_hr), .g(g2_hr));
  convert_bcd convert_bcd_2 (
    .D3(1'b0), .D2(Q13_prime), .D1(Q12_prime), .D0(Q11_prime), .a(a2_min1), .b(b2_min1), .c(c2_min1),
    .d(d2_min1), .e(e2_min1), .f(f2_min1), .g(g2_min1));
  convert_bcd convert_bcd_3 (
    .D3(Q10_prime), .D2(Q9_prime), .D1(Q8_prime), .D0(Q7_prime), .a(a2_min), .b(b2_min), .c(c2_min),
    .d(d2_min), .e(e2_min), .f(f2_min), .g(g2_min));
  convert_bcd convert_bcd_4 (
    .D3(1'b0), .D2(Q6_prime), .D1(Q5_prime), .D0(Q4_prime), .a(a2_sec1), .b(b2_sec1), .c(c2_sec1),
    .d(d2_sec1), .e(e2_sec1), .f(f2_sec1), .g(g2_sec1));
  convert_bcd convert_bcd_5 (
    .D3(Q3_prime), .D2(Q2_prime), .D1(Q1_prime), .D0(Q0_prime), .a(a2_sec), .b(b2_sec), .c(c2_sec),
    .d(d2_sec), .e(e2_sec), .f(f2_sec), .g(g2_sec));
  convert_bcd convert_bcd_6 (
    .D3(Q17), .D2(Q16), .D1(Q15), .D0(Q14), .a(a_hr), .b(b_hr), .c(c_hr), .d(d_hr), .e(e_hr), .f(f_hr),
    .g(g_hr));
  convert_bcd convert_bcd_7 (
    .D3(1'b0), .D2(Q13), .D1(Q12), .D0(Q11), .a(a_min1), .b(b_min1), .c(c_min1), .d(d_min1), .e(e_min1),
    .f(f_min1), .g(g_min1));
  convert_bcd convert_bcd_8 (
    .D3(Q10), .D2(Q9), .D1(Q8), .D0(Q7), .a(a_min), .b(b_min), .c(c_min), .d(d_min), .e(e_min), .f(f_min),
    .g(g_min));
  convert_bcd convert_bcd_9 (
    .D3(1'b0), .D2(Q6), .D1(Q5), .D0(Q4), .a(a_sec1), .b(b_sec1), .c(c_sec1), .d(d_sec1), .e(e_sec1),
    .f(f_sec1), .g(g_sec1));
  convert_bcd convert_bcd_10 (
    .D3(Q3), .D2(Q2), .D1(Q1), .D0(Q0), .a(a_sec), .b(b_sec), .c(c_sec), .d(d_sec), .e(e_sec), .f(f_sec),
    .g(g_sec));
endmodule

module d_ff_updown_v2 (
  input  in_1
);

  wire and_1_out, and_2_out, and_3_out, and_4_out, and_5_out, and_6_out, and_7_out, and_8_out, and_9_out,
       and_10_out, and_11_out, and_12_out, and_13_out, and_14_out, and_15_out, and_16_out, and_17_out,
       and_18_out, and_19_out, and_20_out, and_21_out, and_23_out, and_24_out, and_25_out, and_26_out,
       and_27_out, and_28_out, and_29_out, clock_1_out, clock_2_out, complete_turn_out, convert_bcd_1_a,
       convert_bcd_1_b, convert_bcd_1_c, convert_bcd_1_d, convert_bcd_1_e, convert_bcd_1_f, convert_bcd_1_g,
       convert_bcd_2_a, convert_bcd_2_b, convert_bcd_2_c, convert_bcd_2_d, convert_bcd_2_e, convert_bcd_2_f,
       convert_bcd_2_g, convert_bcd_3_a, convert_bcd_3_b, convert_bcd_3_c, convert_bcd_3_d, convert_bcd_3_e,
       convert_bcd_3_f, convert_bcd_3_g, convert_bcd_4_a, convert_bcd_4_b, convert_bcd_4_c, convert_bcd_4_d,
       convert_bcd_4_e, convert_bcd_4_f, convert_bcd_4_g, d_ff_1_q, d_ff_2_q, d_ff_3_qn, d_ff_4_qn,
       d_ff_5_qn, d_ff_6_qn, mod6_op_1_carry, multiplexer_1_out, multiplexer_2_out, multiplexer_3_out,
       or_1_out, or_2_out, or_3_out, or_4_out, or_5_out, or_6_out, or_7_out, or_8_out, or_9_out, or_10_out,
       or_11_out, or_12_out, or_13_out, or_14_out, or_15_out, or_16_out, pull_resistor_1_node, Q0, Q1, Q2,
       Q3, Q4, Q4N, Q5, Q5N, Q6, Q6N, Q7, Q8, Q9, Q10, Q11, Q12, Q13, RESET, start_out, t_ff_1_q, t_ff_2_q,
       update;

  Clock clock_1 (.out(clock_1_out));
  T_Flip_Flop t_ff_1 (.clk(complete_turn_out), .T(complete_turn_out), .Q(t_ff_1_q));  // open: Qn, preset, reset, en
  and and_1 (and_1_out, t_ff_1_q, ~pull_resistor_1_node);  // AND_Gate
  D_Flip_Flop d_ff_1 (.clk(and_1_out), .D(1'b1), .Q(d_ff_1_q), .reset(d_ff_2_q));  // open: Qn, preset, en
  and and_2 (and_2_out, Q1, Q0);
  and and_3 (and_3_out, Q2, ~Q1, ~Q0);  // AND_Gate
  or or_1 (or_1_out, and_2_out, and_3_out, and_4_out);
  and and_4 (and_4_out, Q3, ~Q0);  // AND_Gate
  or or_2 (or_2_out, and_4_out, and_5_out, and_6_out);
  and and_5 (and_5_out, Q2, Q0);
  and and_6 (and_6_out, Q2, Q1);
  and and_7 (and_7_out, Q3, Q0);
  or or_3 (or_3_out, and_7_out, and_8_out);
  and and_8 (and_8_out, ~Q3, ~Q2, ~Q1, ~Q0);  // AND_Gate
  D_Flip_Flop d_ff_2 (.clk(clock_1_out), .D(d_ff_1_q), .Q(d_ff_2_q));  // open: Qn, preset, en, reset
  and and_9 (and_9_out, Q8, Q7);
  and and_10 (and_10_out, Q9, ~Q8, ~Q7);  // AND_Gate
  or or_4 (or_4_out, and_9_out, and_10_out, and_11_out);
  and and_11 (and_11_out, Q10, ~Q7);  // AND_Gate
  or or_5 (or_5_out, and_11_out, and_12_out, and_13_out);
  and and_12 (and_12_out, Q9, Q7);
  and and_13 (and_13_out, Q9, Q8);
  and and_14 (and_14_out, Q10, Q7);
  or or_6 (or_6_out, and_14_out, and_15_out);
  and and_15 (and_15_out, ~Q10, ~Q9, ~Q8, ~Q7);  // AND_Gate
  Button complete_turn (.out(complete_turn_out));
  Button start (.out(start_out));
  Button u_RESET (.out(RESET));
  or or_7 (or_7_out, complete_turn_out, start_out);
  or or_8 (or_8_out, update, d_ff_2_q);
  D_Flip_Flop d_ff_3 (
    .clk(pull_resistor_1_node), .D(d_ff_3_qn), .Q(Q0), .Qn(d_ff_3_qn), .reset(RESET));  // open: preset, en
  Multiplexer multiplexer_1 (.in0(d_ff_6_qn), .in1(Q4N), .out(multiplexer_1_out), .sel(t_ff_1_q));  // open: en
  D_Flip_Flop d_ff_4 (.clk(and_21_out), .D(d_ff_4_qn), .Q(Q7), .Qn(d_ff_4_qn), .reset(RESET));  // open: preset, en
  D_Flip_Flop d_ff_5 (.clk(and_26_out), .D(d_ff_5_qn), .Q(Q11), .Qn(d_ff_5_qn));  // open: preset, en, reset
  Clock clock_2 (.out(clock_2_out));
  T_Flip_Flop t_ff_2 (.clk(or_7_out), .T(or_7_out), .Q(t_ff_2_q));  // open: Qn, preset, reset, en
  D_Flip_Flop d_ff_6 (.clk(or_8_out), .D(multiplexer_1_out), .Q(Q4), .Qn(d_ff_6_qn));  // open: preset, en, reset
  or or_9 (or_9_out, RESET, update);
  Pull_Resistor pull_resistor_1 (.node(pull_resistor_1_node));
  Transistor #(.\type ("n")) transistor_1 (.in(clock_2_out), .out(pull_resistor_1_node), .gate(t_ff_2_q));
  Multiplexer multiplexer_2 (.in0(or_14_out), .in1(Q5N), .out(multiplexer_2_out), .sel(t_ff_1_q));  // open: en
  D_Flip_Flop d_ff_7 (.clk(and_21_out), .D(or_4_out), .Q(Q8), .reset(or_10_out));  // open: Qn, preset, en
  or or_10 (or_10_out, RESET, and_26_out);
  D_Flip_Flop d_ff_8 (.clk(and_26_out), .D(or_13_out), .Q(Q12), .reset(and_20_out));  // open: Qn, preset, en
  D_Flip_Flop d_ff_9 (.clk(pull_resistor_1_node), .D(or_1_out), .Q(Q1), .reset(or_9_out));  // open: Qn, preset, en
  D_Flip_Flop d_ff_10 (.clk(or_8_out), .D(multiplexer_2_out), .Q(Q5), .reset(and_21_out));  // open: Qn, preset, en
  D_Flip_Flop d_ff_11 (.clk(pull_resistor_1_node), .D(or_2_out), .Q(Q2), .reset(or_11_out));  // open: Qn, preset, en
  or or_11 (or_11_out, RESET, update);
  and and_16 (and_16_out, ~Q4, ~Q5);  // AND_Gate
  and and_17 (and_17_out, Q4, Q5);
  D_Flip_Flop d_ff_12 (.clk(and_21_out), .D(or_5_out), .Q(Q9), .reset(or_12_out));  // open: Qn, preset, en
  or or_12 (or_12_out, RESET, and_26_out);
  and and_18 (and_18_out, ~Q11, ~Q12);  // AND_Gate
  or or_13 (or_13_out, and_18_out, and_19_out);
  and and_19 (and_19_out, Q11, Q12);
  or or_14 (or_14_out, and_16_out, and_17_out);
  Multiplexer multiplexer_3 (.in0(or_15_out), .in1(Q6N), .out(multiplexer_3_out), .sel(t_ff_1_q));  // open: en
  D_Flip_Flop d_ff_13 (.clk(and_26_out), .D(or_16_out), .Q(Q13));  // open: Qn, preset, en, reset
  and and_20 (and_20_out, Q12, Q13);
  D_Flip_Flop d_ff_14 (.clk(pull_resistor_1_node), .D(or_3_out), .Q(Q3), .reset(RESET));  // open: Qn, preset, en
  D_Flip_Flop d_ff_15 (.clk(or_8_out), .D(multiplexer_3_out), .Q(Q6));  // open: Qn, preset, en, reset
  and and_21 (and_21_out, Q6, Q5);
  D_Flip_Flop d_ff_16 (.clk(and_21_out), .D(or_6_out), .Q(Q10), .reset(RESET));  // open: Qn, preset, en
  and and_22 (update, Q0, Q3);
  and and_23 (and_23_out, ~Q6, ~Q4, ~Q5);  // AND_Gate
  and and_24 (and_24_out, Q6, Q4);
  and and_25 (and_25_out, Q6, Q5);
  mod6_op mod6_op_1 (.a(Q6), .b(Q5), .c(Q4), .q1(Q6N), .q2(Q5N), .q3(Q4N), .carry(mod6_op_1_carry));
  and and_26 (and_26_out, Q7, Q10);
  and and_27 (and_27_out, ~Q13, ~Q11, ~Q12);  // AND_Gate
  and and_28 (and_28_out, Q13, Q11);
  and and_29 (and_29_out, Q13, Q12);
  or or_15 (or_15_out, and_23_out, and_24_out, and_25_out);
  or or_16 (or_16_out, and_27_out, and_28_out, and_29_out);
  convert_bcd convert_bcd_1 (
    .D3(Q3), .D2(Q2), .D1(Q1), .D0(Q0), .a(convert_bcd_1_a), .b(convert_bcd_1_b), .c(convert_bcd_1_c),
    .d(convert_bcd_1_d), .e(convert_bcd_1_e), .f(convert_bcd_1_f), .g(convert_bcd_1_g));
  convert_bcd convert_bcd_2 (
    .D3(1'b0), .D2(Q6), .D1(Q5), .D0(Q4), .a(convert_bcd_2_a), .b(convert_bcd_2_b), .c(convert_bcd_2_c),
    .d(convert_bcd_2_d), .e(convert_bcd_2_e), .f(convert_bcd_2_f), .g(convert_bcd_2_g));
  convert_bcd convert_bcd_3 (
    .D3(Q10), .D2(Q9), .D1(Q8), .D0(Q7), .a(convert_bcd_3_a), .b(convert_bcd_3_b), .c(convert_bcd_3_c),
    .d(convert_bcd_3_d), .e(convert_bcd_3_e), .f(convert_bcd_3_f), .g(convert_bcd_3_g));
  convert_bcd convert_bcd_4 (
    .D3(1'b0), .D2(Q13), .D1(Q12), .D0(Q11), .a(convert_bcd_4_a), .b(convert_bcd_4_b), .c(convert_bcd_4_c),
    .d(convert_bcd_4_d), .e(convert_bcd_4_e), .f(convert_bcd_4_f), .g(convert_bcd_4_g));
  _7_Segment_Display #(.active("false")) u_7_segment_display_1 (
    .g(convert_bcd_1_g), .f(convert_bcd_1_f), .a(convert_bcd_1_a), .b(convert_bcd_1_b), .e(convert_bcd_1_e),
    .d(convert_bcd_1_d), .c(convert_bcd_1_c));  // open: dp
  _7_Segment_Display #(.active("false")) u_7_segment_display_2 (
    .g(convert_bcd_2_g), .f(convert_bcd_2_f), .a(convert_bcd_2_a), .b(convert_bcd_2_b), .e(convert_bcd_2_e),
    .d(convert_bcd_2_d), .c(convert_bcd_2_c));  // open: dp
  _7_Segment_Display #(.active("false")) u_7_segment_display_3 (
    .g(convert_bcd_3_g), .f(convert_bcd_3_f), .a(convert_bcd_3_a), .b(convert_bcd_3_b), .e(convert_bcd_3_e),
    .d(convert_bcd_3_d), .c(convert_bcd_3_c));  // open: dp
  _7_Segment_Display #(.active("false")) u_7_segment_display_4 (
    .g(convert_bcd_4_g), .f(convert_bcd_4_f), .a(convert_bcd_4_a), .b(convert_bcd_4_b), .e(convert_bcd_4_e),
    .d(convert_bcd_4_d), .c(convert_bcd_4_c));  // open: dp
endmodule

module mod6_op_new (
  input  add_Sig,
  input  a,
  input  b,
  input  c,
  output q1,
  output q2,
  output q3,
  output carry
);

  wire and_1_out, and_2_out, and_3_out, and_4_out, and_5_out, and_6_out, and_7_out, and_8_out, and_9_out,
       and_10_out, and_11_out, and_12_out, not_1_out, not_2_out, not_3_out, not_4_out, not_5_out, not_6_out,
       not_7_out, not_8_out, not_9_out, not_10_out;

  not not_1 (not_1_out, add_Sig);
  not not_2 (not_2_out, a);
  not not_3 (not_3_out, b);
  not not_4 (not_4_out, c);
  not not_5 (not_5_out, add_Sig);
  not not_6 (not_6_out, a);
  not not_7 (not_7_out, b);
  not not_8 (not_8_out, c);
  not not_9 (not_9_out, add_Sig);
  and and_1 (and_1_out, not_9_out, c);
  and and_2 (and_2_out, add_Sig, not_10_out);
  not not_10 (not_10_out, c);
  and and_3 (and_3_out, add_Sig, a, b);
  and and_4 (and_4_out, add_Sig, b, c);
  and and_5 (and_5_out, add_Sig, a);
  and and_6 (and_6_out, not_1_out, a);
  and and_7 (and_7_out, a, b);
  and and_8 (and_8_out, add_Sig, not_2_out, not_3_out, c);
  and and_9 (and_9_out, add_Sig, b, not_4_out);
  and and_10 (and_10_out, not_5_out, b);
  or or_1 (q2, and_10_out, and_11_out, and_12_out);
  and and_11 (and_11_out, add_Sig, not_6_out, not_7_out, not_8_out);
  and and_12 (and_12_out, add_Sig, a, c);
  or or_2 (q3, and_1_out, and_2_out, and_3_out);
  or or_3 (carry, and_4_out, and_5_out);
  or or_4 (q1, and_6_out, and_7_out, and_8_out, and_9_out);
endmodule

module main1 (
);

  wire COMPLETE_out, d_ff_updown_1_a2_hr, d_ff_updown_1_a2_min, d_ff_updown_1_a2_min1, d_ff_updown_1_a2_sec,
       d_ff_updown_1_a2_sec1, d_ff_updown_1_a_hr, d_ff_updown_1_a_min, d_ff_updown_1_a_min1,
       d_ff_updown_1_a_sec, d_ff_updown_1_a_sec1, d_ff_updown_1_b2_hr, d_ff_updown_1_b2_min,
       d_ff_updown_1_b2_min1, d_ff_updown_1_b2_sec, d_ff_updown_1_b2_sec1, d_ff_updown_1_b_hr,
       d_ff_updown_1_b_min, d_ff_updown_1_b_min1, d_ff_updown_1_b_sec, d_ff_updown_1_b_sec1,
       d_ff_updown_1_c2_hr, d_ff_updown_1_c2_min, d_ff_updown_1_c2_min1, d_ff_updown_1_c2_sec,
       d_ff_updown_1_c2_sec1, d_ff_updown_1_c_hr, d_ff_updown_1_c_min, d_ff_updown_1_c_min1,
       d_ff_updown_1_c_sec, d_ff_updown_1_c_sec1, d_ff_updown_1_d2_hr, d_ff_updown_1_d2_min,
       d_ff_updown_1_d2_min1, d_ff_updown_1_d2_sec, d_ff_updown_1_d2_sec1, d_ff_updown_1_d_hr,
       d_ff_updown_1_d_min, d_ff_updown_1_d_min1, d_ff_updown_1_d_sec, d_ff_updown_1_d_sec1,
       d_ff_updown_1_e2_hr, d_ff_updown_1_e2_min, d_ff_updown_1_e2_min1, d_ff_updown_1_e2_sec,
       d_ff_updown_1_e2_sec1, d_ff_updown_1_e_hr, d_ff_updown_1_e_min, d_ff_updown_1_e_min1,
       d_ff_updown_1_e_sec, d_ff_updown_1_e_sec1, d_ff_updown_1_f2_hr, d_ff_updown_1_f2_min,
       d_ff_updown_1_f2_min1, d_ff_updown_1_f2_sec, d_ff_updown_1_f2_sec1, d_ff_updown_1_f_hr,
       d_ff_updown_1_f_min, d_ff_updown_1_f_min1, d_ff_updown_1_f_sec, d_ff_updown_1_f_sec1,
       d_ff_updown_1_g2_hr, d_ff_updown_1_g2_min, d_ff_updown_1_g2_min1, d_ff_updown_1_g2_sec,
       d_ff_updown_1_g2_sec1, d_ff_updown_1_g_hr, d_ff_updown_1_g_min, d_ff_updown_1_g_min1,
       d_ff_updown_1_g_sec, d_ff_updown_1_g_sec1, RESET_out, START_out;

  _7_Segment_Display #(.active("false")) u_7_segment_display_1 (
    .g(d_ff_updown_1_g_hr), .f(d_ff_updown_1_f_hr), .a(d_ff_updown_1_a_hr), .b(d_ff_updown_1_b_hr),
    .e(d_ff_updown_1_e_hr), .d(d_ff_updown_1_d_hr), .c(d_ff_updown_1_c_hr));  // open: dp
  _7_Segment_Display #(.active("false")) u_7_segment_display_2 (
    .g(1'b1), .f(1'b0), .a(1'b0), .b(1'b0), .e(1'b0), .d(1'b0), .c(1'b0));  // open: dp
  _7_Segment_Display #(.active("false")) u_7_segment_display_3 (
    .g(d_ff_updown_1_g_min1), .f(d_ff_updown_1_f_min1), .a(d_ff_updown_1_a_min1), .b(d_ff_updown_1_b_min1),
    .e(d_ff_updown_1_e_min1), .d(d_ff_updown_1_d_min1), .c(d_ff_updown_1_c_min1));  // open: dp
  _7_Segment_Display #(.active("false")) u_7_segment_display_4 (
    .g(d_ff_updown_1_g_min), .f(d_ff_updown_1_f_min), .a(d_ff_updown_1_a_min), .b(d_ff_updown_1_b_min),
    .e(d_ff_updown_1_e_min), .d(d_ff_updown_1_d_min), .c(d_ff_updown_1_c_min));  // open: dp
  Button RESET (.out(RESET_out));
  _7_Segment_Display #(.active("false")) u_7_segment_display_5 (
    .g(d_ff_updown_1_g_sec1), .f(d_ff_updown_1_f_sec1), .a(d_ff_updown_1_a_sec1), .b(d_ff_updown_1_b_sec1),
    .e(d_ff_updown_1_e_sec1), .d(d_ff_updown_1_d_sec1), .c(d_ff_updown_1_c_sec1));  // open: dp
  _7_Segment_Display #(.active("false")) u_7_segment_display_6 (
    .g(d_ff_updown_1_g_sec), .f(d_ff_updown_1_f_sec), .a(d_ff_updown_1_a_sec), .b(d_ff_updown_1_b_sec),
    .e(d_ff_updown_1_e_sec), .d(d_ff_updown_1_d_sec), .c(d_ff_updown_1_c_sec));  // open: dp
  Button COMPLETE (.out(COMPLETE_out));
  Button START (.out(START_out));
  _7_Segment_Display #(.active("false")) u_7_segment_display_7 (
    .g(d_ff_updown_1_g2_hr), .f(d_ff_updown_1_f2_hr), .a(d_ff_updown_1_a2_hr), .b(d_ff_updown_1_b2_hr),
    .e(d_ff_updown_1_e2_hr), .d(d_ff_updown_1_d2_hr), .c(d_ff_updown_1_c2_hr));  // open: dp
  _7_Segment_Display #(.active("false")) u_7_segment_display_8 (
    .g(1'b1), .f(1'b0), .a(1'b0), .b(1'b0), .e(1'b0), .d(1'b0), .c(1'b0));  // open: dp
  d_ff_updown d_ff_updown_1 (
    .complete_turn(COMPLETE_out), .start(START_out), .RESET(RESET_out), .a2_hr(d_ff_updown_1_a2_hr),
    .b2_hr(d_ff_updown_1_b2_hr), .c2_hr(d_ff_updown_1_c2_hr), .d2_hr(d_ff_updown_1_d2_hr),
    .e2_hr(d_ff_updown_1_e2_hr), .f2_hr(d_ff_updown_1_f2_hr), .g2_hr(d_ff_updown_1_g2_hr),
    .a2_min1(d_ff_updown_1_a2_min1), .b2_min1(d_ff_updown_1_b2_min1), .c2_min1(d_ff_updown_1_c2_min1),
    .d2_min1(d_ff_updown_1_d2_min1), .e2_min1(d_ff_updown_1_e2_min1), .f2_min1(d_ff_updown_1_f2_min1),
    .g2_min1(d_ff_updown_1_g2_min1), .a2_min(d_ff_updown_1_a2_min), .b2_min(d_ff_updown_1_b2_min),
    .c2_min(d_ff_updown_1_c2_min), .d2_min(d_ff_updown_1_d2_min), .e2_min(d_ff_updown_1_e2_min),
    .f2_min(d_ff_updown_1_f2_min), .g2_min(d_ff_updown_1_g2_min), .a2_sec1(d_ff_updown_1_a2_sec1),
    .b2_sec1(d_ff_updown_1_b2_sec1), .c2_sec1(d_ff_updown_1_c2_sec1), .d2_sec1(d_ff_updown_1_d2_sec1),
    .e2_sec1(d_ff_updown_1_e2_sec1), .f2_sec1(d_ff_updown_1_f2_sec1), .g2_sec1(d_ff_updown_1_g2_sec1),
    .a2_sec(d_ff_updown_1_a2_sec), .b2_sec(d_ff_updown_1_b2_sec), .c2_sec(d_ff_updown_1_c2_sec),
    .d2_sec(d_ff_updown_1_d2_sec), .e2_sec(d_ff_updown_1_e2_sec), .f2_sec(d_ff_updown_1_f2_sec),
    .g2_sec(d_ff_updown_1_g2_sec), .a_hr(d_ff_updown_1_a_hr), .b_hr(d_ff_updown_1_b_hr),
    .c_hr(d_ff_updown_1_c_hr), .d_hr(d_ff_updown_1_d_hr), .e_hr(d_ff_updown_1_e_hr),
    .f_hr(d_ff_updown_1_f_hr), .g_hr(d_ff_updown_1_g_hr), .a_min1(d_ff_updown_1_a_min1),
    .b_min1(d_ff_updown_1_b_min1), .c_min1(d_ff_updown_1_c_min1), .d_min1(d_ff_updown_1_d_min1),
    .e_min1(d_ff_updown_1_e_min1), .f_min1(d_ff_updown_1_f_min1), .g_min1(d_ff_updown_1_g_min1),
    .a_min(d_ff_updown_1_a_min), .b_min(d_ff_updown_1_b_min), .c_min(d_ff_updown_1_c_min),
    .d_min(d_ff_updown_1_d_min), .e_min(d_ff_updown_1_e_min), .f_min(d_ff_updown_1_f_min),
    .g_min(d_ff_updown_1_g_min), .a_sec1(d_ff_updown_1_a_sec1), .b_sec1(d_ff_updown_1_b_sec1),
    .c_sec1(d_ff_updown_1_c_sec1), .d_sec1(d_ff_updown_1_d_sec1), .e_sec1(d_ff_updown_1_e_sec1),
    .f_sec1(d_ff_updown_1_f_sec1), .g_sec1(d_ff_updown_1_g_sec1), .a_sec(d_ff_updown_1_a_sec),
    .b_sec(d_ff_updown_1_b_sec), .c_sec(d_ff_updown_1_c_sec), .d_sec(d_ff_updown_1_d_sec),
    .e_sec(d_ff_updown_1_e_sec), .f_sec(d_ff_updown_1_f_sec), .g_sec(d_ff_updown_1_g_sec));
  _7_Segment_Display #(.active("false")) u_7_segment_display_9 (
    .g(d_ff_updown_1_g2_min1), .f(d_ff_updown_1_f2_min1), .a(d_ff_updown_1_a2_min1),
    .b(d_ff_updown_1_b2_min1), .e(d_ff_updown_1_e2_min1), .d(d_ff_updown_1_d2_min1), .c(d_ff_updown_1_c2_min1));  // open: dp
  _7_Segment_Display #(.active("false")) u_7_segment_display_10 (
    .g(d_ff_updown_1_g2_min), .f(d_ff_updown_1_f2_min), .a(d_ff_updown_1_a2_min), .b(d_ff_updown_1_b2_min),
    .e(d_ff_updown_1_e2_min), .d(d_ff_updown_1_d2_min), .c(d_ff_updown_1_c2_min));  // open: dp
  _7_Segment_Display #(.active("false")) u_7_segment_display_11 (
    .g(d_ff_updown_1_g2_sec), .f(d_ff_updown_1_f2_sec), .a(d_ff_updown_1_a2_sec), .b(d_ff_updown_1_b2_sec),
    .e(d_ff_updown_1_e2_sec), .d(d_ff_updown_1_d2_sec), .c(d_ff_updown_1_c2_sec));  // open: dp
  _7_Segment_Display #(.active("false")) u_7_segment_display_12 (
    .g(d_ff_updown_1_g2_sec1), .f(d_ff_updown_1_f2_sec1), .a(d_ff_updown_1_a2_sec1),
    .b(d_ff_updown_1_b2_sec1), .e(d_ff_updown_1_e2_sec1), .d(d_ff_updown_1_d2_sec1), .c(d_ff_updown_1_c2_sec1));  // open: dp
endmodule
